// Logisim project 16_byte_ram.circ as structural Verilog: 4 circuits, main circuit RAM
module Byte (
  input  Read_write,
  input  in_2,
  input  in_3,
  input  in_4,
  input  in_5,
  input  in_6,
  input  in_7,
  input  in_8,
  input  in_9,
  input  in_10,
  output out_11,
  output out_12,
  output out_13,
  output out_14,
  output out_15,
  output out_16,
  output out_17,
  output out_18
);

  wire multiplexer_1_out, multiplexer_2_out, multiplexer_3_out, multiplexer_4_out, multiplexer_5_out,
       multiplexer_6_out, multiplexer_7_out, multiplexer_8_out, not_1_out, or_1_out;

  or or_1 (or_1_out, in_2, Read_write);
  not not_1 (not_1_out, in_2);
  Multiplexer #(.enable("false")) multiplexer_1 (.in0(in_3), .in1(not_1_out), .out(multiplexer_1_out), .sel(in_2));
  Multiplexer #(.enable("false")) multiplexer_2 (.in0(in_4), .in1(not_1_out), .out(multiplexer_2_out), .sel(in_2));
  Multiplexer #(.enable("false")) multiplexer_3 (.in0(in_5), .in1(not_1_out), .out(multiplexer_3_out), .sel(in_2));
  Multiplexer #(.enable("false")) multiplexer_4 (.in0(in_6), .in1(not_1_out), .out(multiplexer_4_out), .sel(in_2));
  Multiplexer #(.enable("false")) multiplexer_5 (.in0(in_7), .in1(not_1_out), .out(multiplexer_5_out), .sel(in_2));
  Multiplexer #(.enable("false")) multiplexer_6 (.in0(in_8), .in1(not_1_out), .out(multiplexer_6_out), .sel(in_2));
  Multiplexer #(.enable("false")) multiplexer_7 (.in0(in_9), .in1(not_1_out), .out(multiplexer_7_out), .sel(in_2));
  D_Flip_Flop d_ff_1 (.clk(or_1_out), .D(multiplexer_7_out), .Q(out_17), .reset(in_2));  // open: Qn, preset, en
  D_Flip_Flop d_ff_2 (.clk(or_1_out), .D(multiplexer_8_out), .Q(out_18), .reset(in_2));  // open: Qn, preset, en
  Multiplexer #(.enable("false")) multiplexer_8 (.in0(in_10), .in1(not_1_out), .out(multiplexer_8_out), .sel(in_2));
  D_Flip_Flop d_ff_3 (.clk(or_1_out), .D(multiplexer_1_out), .Q(out_11), .reset(in_2));  // open: Qn, preset, en
  D_Flip_Flop d_ff_4 (.clk(or_1_out), .D(multiplexer_2_out), .Q(out_12), .reset(in_2));  // open: Qn, preset, en
  D_Flip_Flop d_ff_5 (.clk(or_1_out), .D(multiplexer_3_out), .Q(out_13), .reset(in_2));  // open: Qn, preset, en
  D_Flip_Flop d_ff_6 (.clk(or_1_out), .D(multiplexer_4_out), .Q(out_14), .reset(in_2));  // open: Qn, preset, en
  D_Flip_Flop d_ff_7 (.clk(or_1_out), .D(multiplexer_5_out), .Q(out_15), .reset(in_2));  // open: Qn, preset, en
  D_Flip_Flop d_ff_8 (.clk(or_1_out), .D(multiplexer_6_out), .Q(out_16), .reset(in_2));  // open: Qn, preset, en

  // Notes on the sheet:
  //   CLEAR
endmodule

module RAM (
  input  Clock,
  input  Read_Write,
  input  in_3,
  input  in_4,
  input  Address,
  input  in_6,
  input  in_7,
  input  in_8,
  input  in_9,
  input  in_10,
  input  in_11,
  input  in_12,
  input  in_13,
  input  in_14,
  input  CLEAR,
  output out_16,
  output out_17,
  output out_18,
  output out_19,
  output out_20,
  output out_21,
  output out_22,
  output out_23
);

  wire and_1_out, and_2_out, and_3_out, and_4_out, and_5_out, and_6_out, and_7_out, and_8_out, and_9_out,
       and_10_out, and_11_out, and_12_out, and_13_out, and_14_out, and_15_out, and_16_out, and_17_out,
       and_18_out, and_19_out, and_20_out, and_21_out, and_22_out, and_23_out, and_24_out, and_25_out,
       and_26_out, and_27_out, and_28_out, and_29_out, and_30_out, and_31_out, and_32_out, and_33_out,
       and_34_out, and_35_out, and_36_out, and_37_out, and_38_out, and_39_out, and_40_out, and_41_out,
       and_42_out, and_43_out, and_44_out, and_45_out, and_46_out, and_47_out, and_48_out, and_49_out,
       byte_1_out_11, byte_1_out_12, byte_1_out_13, byte_1_out_14, byte_1_out_15, byte_1_out_16,
       byte_1_out_17, byte_1_out_18, byte_2_out_11, byte_2_out_12, byte_2_out_13, byte_2_out_14,
       byte_2_out_15, byte_2_out_16, byte_2_out_17, byte_2_out_18, byte_3_out_11, byte_3_out_12,
       byte_3_out_13, byte_3_out_14, byte_3_out_15, byte_3_out_16, byte_3_out_17, byte_3_out_18,
       byte_4_out_11, byte_4_out_12, byte_4_out_13, byte_4_out_14, byte_4_out_15, byte_4_out_16,
       byte_4_out_17, byte_4_out_18, byte_5_out_11, byte_5_out_12, byte_5_out_13, byte_5_out_14,
       byte_5_out_15, byte_5_out_16, byte_5_out_17, byte_5_out_18, byte_6_out_11, byte_6_out_12,
       byte_6_out_13, byte_6_out_14, byte_6_out_15, byte_6_out_16, byte_6_out_17, byte_6_out_18,
       byte_7_out_11, byte_7_out_12, byte_7_out_13, byte_7_out_14, byte_7_out_15, byte_7_out_16,
       byte_7_out_17, byte_7_out_18, byte_8_out_11, byte_8_out_12, byte_8_out_13, byte_8_out_14,
       byte_8_out_15, byte_8_out_16, byte_8_out_17, byte_8_out_18, byte_9_out_11, byte_9_out_12,
       byte_9_out_13, byte_9_out_14, byte_9_out_15, byte_9_out_16, byte_9_out_17, byte_9_out_18,
       byte_10_out_11, byte_10_out_12, byte_10_out_13, byte_10_out_14, byte_10_out_15, byte_10_out_16,
       byte_10_out_17, byte_10_out_18, byte_11_out_11, byte_11_out_12, byte_11_out_13, byte_11_out_14,
       byte_11_out_15, byte_11_out_16, byte_11_out_17, byte_11_out_18, byte_12_out_11, byte_12_out_12,
       byte_12_out_13, byte_12_out_14, byte_12_out_15, byte_12_out_16, byte_12_out_17, byte_12_out_18,
       byte_13_out_11, byte_13_out_12, byte_13_out_13, byte_13_out_14, byte_13_out_15, byte_13_out_16,
       byte_13_out_17, byte_13_out_18, byte_14_out_11, byte_14_out_12, byte_14_out_13, byte_14_out_14,
       byte_14_out_15, byte_14_out_16, byte_14_out_17, byte_14_out_18, byte_15_out_11, byte_15_out_12,
       byte_15_out_13, byte_15_out_14, byte_15_out_15, byte_15_out_16, byte_15_out_17, byte_15_out_18,
       byte_16_out_11, byte_16_out_12, byte_16_out_13, byte_16_out_14, byte_16_out_15, byte_16_out_16,
       byte_16_out_17, byte_16_out_18, not_1_out, not_2_out, not_3_out, not_4_out, not_5_out, not_6_out,
       not_7_out, not_8_out, not_9_out, not_10_out, not_11_out, not_12_out, not_13_out, not_14_out,
       not_15_out, not_16_out, not_17_out, not_18_out, not_19_out, not_20_out, not_21_out, not_22_out,
       not_23_out, not_24_out, not_25_out, not_26_out, not_27_out, not_28_out, not_29_out,
       read_stopper_1_out_10, read_stopper_1_out_11, read_stopper_1_out_12, read_stopper_1_out_13,
       read_stopper_1_out_14, read_stopper_1_out_15, read_stopper_1_out_16, read_stopper_1_out_17,
       read_stopper_2_out_10, read_stopper_2_out_11, read_stopper_2_out_12, read_stopper_2_out_13,
       read_stopper_2_out_14, read_stopper_2_out_15, read_stopper_2_out_16, read_stopper_2_out_17,
       read_stopper_3_out_10, read_stopper_3_out_11, read_stopper_3_out_12, read_stopper_3_out_13,
       read_stopper_3_out_14, read_stopper_3_out_15, read_stopper_3_out_16, read_stopper_3_out_17,
       read_stopper_4_out_10, read_stopper_4_out_11, read_stopper_4_out_12, read_stopper_4_out_13,
       read_stopper_4_out_14, read_stopper_4_out_15, read_stopper_4_out_16, read_stopper_4_out_17,
       read_stopper_5_out_10, read_stopper_5_out_11, read_stopper_5_out_12, read_stopper_5_out_13,
       read_stopper_5_out_14, read_stopper_5_out_15, read_stopper_5_out_16, read_stopper_5_out_17,
       read_stopper_6_out_10, read_stopper_6_out_11, read_stopper_6_out_12, read_stopper_6_out_13,
       read_stopper_6_out_14, read_stopper_6_out_15, read_stopper_6_out_16, read_stopper_6_out_17,
       read_stopper_7_out_10, read_stopper_7_out_11, read_stopper_7_out_12, read_stopper_7_out_13,
       read_stopper_7_out_14, read_stopper_7_out_15, read_stopper_7_out_16, read_stopper_7_out_17,
       read_stopper_8_out_10, read_stopper_8_out_11, read_stopper_8_out_12, read_stopper_8_out_13,
       read_stopper_8_out_14, read_stopper_8_out_15, read_stopper_8_out_16, read_stopper_8_out_17,
       read_stopper_9_out_10, read_stopper_9_out_11, read_stopper_9_out_12, read_stopper_9_out_13,
       read_stopper_9_out_14, read_stopper_9_out_15, read_stopper_9_out_16, read_stopper_9_out_17,
       read_stopper_10_out_10, read_stopper_10_out_11, read_stopper_10_out_12, read_stopper_10_out_13,
       read_stopper_10_out_14, read_stopper_10_out_15, read_stopper_10_out_16, read_stopper_10_out_17,
       read_stopper_11_out_10, read_stopper_11_out_11, read_stopper_11_out_12, read_stopper_11_out_13,
       read_stopper_11_out_14, read_stopper_11_out_15, read_stopper_11_out_16, read_stopper_11_out_17,
       read_stopper_12_out_10, read_stopper_12_out_11, read_stopper_12_out_12, read_stopper_12_out_13,
       read_stopper_12_out_14, read_stopper_12_out_15, read_stopper_12_out_16, read_stopper_12_out_17,
       read_stopper_13_out_10, read_stopper_13_out_11, read_stopper_13_out_12, read_stopper_13_out_13,
       read_stopper_13_out_14, read_stopper_13_out_15, read_stopper_13_out_16, read_stopper_13_out_17,
       read_stopper_14_out_10, read_stopper_14_out_11, read_stopper_14_out_12, read_stopper_14_out_13,
       read_stopper_14_out_14, read_stopper_14_out_15, read_stopper_14_out_16, read_stopper_14_out_17,
       read_stopper_15_out_10, read_stopper_15_out_11, read_stopper_15_out_12, read_stopper_15_out_13,
       read_stopper_15_out_14, read_stopper_15_out_15, read_stopper_15_out_16, read_stopper_15_out_17,
       read_stopper_16_out_10, read_stopper_16_out_11, read_stopper_16_out_12, read_stopper_16_out_13,
       read_stopper_16_out_14, read_stopper_16_out_15, read_stopper_16_out_16, read_stopper_16_out_17;

  not not_1 (not_1_out, in_3);
  not not_2 (not_2_out, Address);
  not not_3 (not_3_out, Address);
  not not_4 (not_4_out, Address);
  not not_5 (not_5_out, Address);
  not not_6 (not_6_out, in_6);
  not not_7 (not_7_out, in_4);
  not not_8 (not_8_out, in_4);
  not not_9 (not_9_out, in_6);
  not not_10 (not_10_out, in_4);
  not not_11 (not_11_out, in_4);
  not not_12 (not_12_out, in_6);
  not not_13 (not_13_out, in_6);
  not not_14 (not_14_out, in_6);
  not not_15 (not_15_out, not_1_out);
  not not_16 (not_16_out, in_4);
  not not_17 (not_17_out, not_1_out);
  not not_18 (not_18_out, in_4);
  not not_19 (not_19_out, in_6);
  not not_20 (not_20_out, not_1_out);
  not not_21 (not_21_out, in_4);
  not not_22 (not_22_out, not_1_out);
  not not_23 (not_23_out, in_4);
  not not_24 (not_24_out, in_6);
  not not_25 (not_25_out, not_1_out);
  not not_26 (not_26_out, not_1_out);
  not not_27 (not_27_out, in_6);
  not not_28 (not_28_out, not_1_out);
  not not_29 (not_29_out, not_1_out);
  and and_1 (and_1_out, not_2_out, not_6_out, not_1_out, not_7_out);
  and and_2 (and_2_out, not_2_out, in_6, not_1_out, not_8_out);
  and and_3 (and_3_out, Address, not_9_out, not_1_out, not_10_out);
  and and_4 (and_4_out, in_6, Address, not_1_out, not_11_out);
  and and_5 (and_5_out, not_3_out, not_12_out, not_1_out, in_4);
  and and_6 (and_6_out, not_3_out, in_6, not_1_out, in_4);
  and and_7 (and_7_out, Address, not_13_out, not_1_out, in_4);
  and and_8 (and_8_out, in_6, Address, not_1_out, in_4);
  and and_9 (and_9_out, not_4_out, not_14_out, not_15_out, not_16_out);
  and and_10 (and_10_out, not_4_out, in_6, not_17_out, not_18_out);
  and and_11 (and_11_out, Address, not_19_out, not_20_out, not_21_out);
  and and_12 (and_12_out, in_6, Address, not_22_out, not_23_out);
  and and_13 (and_13_out, not_5_out, not_24_out, not_25_out, in_4);
  and and_14 (and_14_out, not_5_out, in_6, not_26_out, in_4);
  and and_15 (and_15_out, Address, not_27_out, not_28_out, in_4);
  and and_16 (and_16_out, in_6, Address, not_29_out, in_4);
  and and_17 (and_17_out, Clock, Read_Write);
  and and_18 (and_18_out, and_1_out, 1'b1);
  and and_19 (and_19_out, and_1_out, and_17_out);
  Byte byte_1 (
    .in_6(in_10), .in_5(in_9), .in_4(in_8), .in_3(in_7), .out_11(byte_1_out_11), .out_12(byte_1_out_12),
    .out_13(byte_1_out_13), .out_14(byte_1_out_14), .Read_write(and_19_out), .in_7(in_11), .in_8(in_12),
    .in_9(in_13), .in_10(in_14), .out_15(byte_1_out_15), .out_16(byte_1_out_16), .out_17(byte_1_out_17),
    .out_18(byte_1_out_18), .in_2(CLEAR));
  Read_Stopper read_stopper_1 (
    .in_2(byte_1_out_11), .in_3(byte_1_out_12), .in_4(byte_1_out_13), .in_5(byte_1_out_14),
    .out_10(read_stopper_1_out_10), .out_11(read_stopper_1_out_11), .out_12(read_stopper_1_out_12),
    .out_13(read_stopper_1_out_13), .in_6(byte_1_out_15), .in_7(byte_1_out_16), .in_8(byte_1_out_17),
    .in_9(byte_1_out_18), .out_14(read_stopper_1_out_14), .out_15(read_stopper_1_out_15),
    .out_16(read_stopper_1_out_16), .out_17(read_stopper_1_out_17), .in_1(and_18_out));
  and and_20 (and_20_out, and_2_out, 1'b1);
  and and_21 (and_21_out, and_2_out, and_17_out);
  Byte byte_2 (
    .in_6(in_10), .in_5(in_9), .in_4(in_8), .in_3(in_7), .out_11(byte_2_out_11), .out_12(byte_2_out_12),
    .out_13(byte_2_out_13), .out_14(byte_2_out_14), .Read_write(and_21_out), .in_7(in_11), .in_8(in_12),
    .in_9(in_13), .in_10(in_14), .out_15(byte_2_out_15), .out_16(byte_2_out_16), .out_17(byte_2_out_17),
    .out_18(byte_2_out_18), .in_2(CLEAR));
  Read_Stopper read_stopper_2 (
    .in_2(byte_2_out_11), .in_3(byte_2_out_12), .in_4(byte_2_out_13), .in_5(byte_2_out_14),
    .out_10(read_stopper_2_out_10), .out_11(read_stopper_2_out_11), .out_12(read_stopper_2_out_12),
    .out_13(read_stopper_2_out_13), .in_6(byte_2_out_15), .in_7(byte_2_out_16), .in_8(byte_2_out_17),
    .in_9(byte_2_out_18), .out_14(read_stopper_2_out_14), .out_15(read_stopper_2_out_15),
    .out_16(read_stopper_2_out_16), .out_17(read_stopper_2_out_17), .in_1(and_20_out));
  and and_22 (and_22_out, and_3_out, 1'b1);
  and and_23 (and_23_out, and_3_out, and_17_out);
  Byte byte_3 (
    .in_6(in_10), .in_5(in_9), .in_4(in_8), .in_3(in_7), .out_11(byte_3_out_11), .out_12(byte_3_out_12),
    .out_13(byte_3_out_13), .out_14(byte_3_out_14), .Read_write(and_23_out), .in_7(in_11), .in_8(in_12),
    .in_9(in_13), .in_10(in_14), .out_15(byte_3_out_15), .out_16(byte_3_out_16), .out_17(byte_3_out_17),
    .out_18(byte_3_out_18), .in_2(CLEAR));
  Read_Stopper read_stopper_3 (
    .in_2(byte_3_out_11), .in_3(byte_3_out_12), .in_4(byte_3_out_13), .in_5(byte_3_out_14),
    .out_10(read_stopper_3_out_10), .out_11(read_stopper_3_out_11), .out_12(read_stopper_3_out_12),
    .out_13(read_stopper_3_out_13), .in_6(byte_3_out_15), .in_7(byte_3_out_16), .in_8(byte_3_out_17),
    .in_9(byte_3_out_18), .out_14(read_stopper_3_out_14), .out_15(read_stopper_3_out_15),
    .out_16(read_stopper_3_out_16), .out_17(read_stopper_3_out_17), .in_1(and_22_out));
  and and_24 (and_24_out, and_4_out, 1'b1);
  and and_25 (and_25_out, and_4_out, and_17_out);
  Byte byte_4 (
    .in_6(in_10), .in_5(in_9), .in_4(in_8), .in_3(in_7), .out_11(byte_4_out_11), .out_12(byte_4_out_12),
    .out_13(byte_4_out_13), .out_14(byte_4_out_14), .Read_write(and_25_out), .in_7(in_11), .in_8(in_12),
    .in_9(in_13), .in_10(in_14), .out_15(byte_4_out_15), .out_16(byte_4_out_16), .out_17(byte_4_out_17),
    .out_18(byte_4_out_18), .in_2(CLEAR));
  Read_Stopper read_stopper_4 (
    .in_2(byte_4_out_11), .in_3(byte_4_out_12), .in_4(byte_4_out_13), .in_5(byte_4_out_14),
    .out_10(read_stopper_4_out_10), .out_11(read_stopper_4_out_11), .out_12(read_stopper_4_out_12),
    .out_13(read_stopper_4_out_13), .in_6(byte_4_out_15), .in_7(byte_4_out_16), .in_8(byte_4_out_17),
    .in_9(byte_4_out_18), .out_14(read_stopper_4_out_14), .out_15(read_stopper_4_out_15),
    .out_16(read_stopper_4_out_16), .out_17(read_stopper_4_out_17), .in_1(and_24_out));
  and and_26 (and_26_out, and_5_out, 1'b1);
  and and_27 (and_27_out, and_5_out, and_17_out);
  Byte byte_5 (
    .in_6(in_10), .in_5(in_9), .in_4(in_8), .in_3(in_7), .out_11(byte_5_out_11), .out_12(byte_5_out_12),
    .out_13(byte_5_out_13), .out_14(byte_5_out_14), .Read_write(and_27_out), .in_7(in_11), .in_8(in_12),
    .in_9(in_13), .in_10(in_14), .out_15(byte_5_out_15), .out_16(byte_5_out_16), .out_17(byte_5_out_17),
    .out_18(byte_5_out_18), .in_2(CLEAR));
  Read_Stopper read_stopper_5 (
    .in_2(byte_5_out_11), .in_3(byte_5_out_12), .in_4(byte_5_out_13), .in_5(byte_5_out_14),
    .out_10(read_stopper_5_out_10), .out_11(read_stopper_5_out_11), .out_12(read_stopper_5_out_12),
    .out_13(read_stopper_5_out_13), .in_6(byte_5_out_15), .in_7(byte_5_out_16), .in_8(byte_5_out_17),
    .in_9(byte_5_out_18), .out_14(read_stopper_5_out_14), .out_15(read_stopper_5_out_15),
    .out_16(read_stopper_5_out_16), .out_17(read_stopper_5_out_17), .in_1(and_26_out));
  and and_28 (and_28_out, and_6_out, 1'b1);
  and and_29 (and_29_out, and_6_out, and_17_out);
  Byte byte_6 (
    .in_6(in_10), .in_5(in_9), .in_4(in_8), .in_3(in_7), .out_11(byte_6_out_11), .out_12(byte_6_out_12),
    .out_13(byte_6_out_13), .out_14(byte_6_out_14), .Read_write(and_29_out), .in_7(in_11), .in_8(in_12),
    .in_9(in_13), .in_10(in_14), .out_15(byte_6_out_15), .out_16(byte_6_out_16), .out_17(byte_6_out_17),
    .out_18(byte_6_out_18), .in_2(CLEAR));
  Read_Stopper read_stopper_6 (
    .in_2(byte_6_out_11), .in_3(byte_6_out_12), .in_4(byte_6_out_13), .in_5(byte_6_out_14),
    .out_10(read_stopper_6_out_10), .out_11(read_stopper_6_out_11), .out_12(read_stopper_6_out_12),
    .out_13(read_stopper_6_out_13), .in_6(byte_6_out_15), .in_7(byte_6_out_16), .in_8(byte_6_out_17),
    .in_9(byte_6_out_18), .out_14(read_stopper_6_out_14), .out_15(read_stopper_6_out_15),
    .out_16(read_stopper_6_out_16), .out_17(read_stopper_6_out_17), .in_1(and_28_out));
  and and_30 (and_30_out, and_7_out, 1'b1);
  and and_31 (and_31_out, and_7_out, and_17_out);
  Byte byte_7 (
    .in_6(in_10), .in_5(in_9), .in_4(in_8), .in_3(in_7), .out_11(byte_7_out_11), .out_12(byte_7_out_12),
    .out_13(byte_7_out_13), .out_14(byte_7_out_14), .Read_write(and_31_out), .in_7(in_11), .in_8(in_12),
    .in_9(in_13), .in_10(in_14), .out_15(byte_7_out_15), .out_16(byte_7_out_16), .out_17(byte_7_out_17),
    .out_18(byte_7_out_18), .in_2(CLEAR));
  Read_Stopper read_stopper_7 (
    .in_2(byte_7_out_11), .in_3(byte_7_out_12), .in_4(byte_7_out_13), .in_5(byte_7_out_14),
    .out_10(read_stopper_7_out_10), .out_11(read_stopper_7_out_11), .out_12(read_stopper_7_out_12),
    .out_13(read_stopper_7_out_13), .in_6(byte_7_out_15), .in_7(byte_7_out_16), .in_8(byte_7_out_17),
    .in_9(byte_7_out_18), .out_14(read_stopper_7_out_14), .out_15(read_stopper_7_out_15),
    .out_16(read_stopper_7_out_16), .out_17(read_stopper_7_out_17), .in_1(and_30_out));
  and and_32 (and_32_out, and_8_out, 1'b1);
  and and_33 (and_33_out, and_8_out, and_17_out);
  Byte byte_8 (
    .in_6(in_10), .in_5(in_9), .in_4(in_8), .in_3(in_7), .out_11(byte_8_out_11), .out_12(byte_8_out_12),
    .out_13(byte_8_out_13), .out_14(byte_8_out_14), .Read_write(and_33_out), .in_7(in_11), .in_8(in_12),
    .in_9(in_13), .in_10(in_14), .out_15(byte_8_out_15), .out_16(byte_8_out_16), .out_17(byte_8_out_17),
    .out_18(byte_8_out_18), .in_2(CLEAR));
  Read_Stopper read_stopper_8 (
    .in_2(byte_8_out_11), .in_3(byte_8_out_12), .in_4(byte_8_out_13), .in_5(byte_8_out_14),
    .out_10(read_stopper_8_out_10), .out_11(read_stopper_8_out_11), .out_12(read_stopper_8_out_12),
    .out_13(read_stopper_8_out_13), .in_6(byte_8_out_15), .in_7(byte_8_out_16), .in_8(byte_8_out_17),
    .in_9(byte_8_out_18), .out_14(read_stopper_8_out_14), .out_15(read_stopper_8_out_15),
    .out_16(read_stopper_8_out_16), .out_17(read_stopper_8_out_17), .in_1(and_32_out));
  and and_34 (and_34_out, and_9_out, 1'b1);
  and and_35 (and_35_out, and_9_out, and_17_out);
  Byte byte_9 (
    .in_6(in_10), .in_5(in_9), .in_4(in_8), .in_3(in_7), .out_11(byte_9_out_11), .out_12(byte_9_out_12),
    .out_13(byte_9_out_13), .out_14(byte_9_out_14), .Read_write(and_35_out), .in_7(in_11), .in_8(in_12),
    .in_9(in_13), .in_10(in_14), .out_15(byte_9_out_15), .out_16(byte_9_out_16), .out_17(byte_9_out_17),
    .out_18(byte_9_out_18), .in_2(CLEAR));
  Read_Stopper read_stopper_9 (
    .in_2(byte_9_out_11), .in_3(byte_9_out_12), .in_4(byte_9_out_13), .in_5(byte_9_out_14),
    .out_10(read_stopper_9_out_10), .out_11(read_stopper_9_out_11), .out_12(read_stopper_9_out_12),
    .out_13(read_stopper_9_out_13), .in_6(byte_9_out_15), .in_7(byte_9_out_16), .in_8(byte_9_out_17),
    .in_9(byte_9_out_18), .out_14(read_stopper_9_out_14), .out_15(read_stopper_9_out_15),
    .out_16(read_stopper_9_out_16), .out_17(read_stopper_9_out_17), .in_1(and_34_out));
  and and_36 (and_36_out, and_10_out, 1'b1);
  and and_37 (and_37_out, and_10_out, and_17_out);
  Byte byte_10 (
    .in_6(in_10), .in_5(in_9), .in_4(in_8), .in_3(in_7), .out_11(byte_10_out_11), .out_12(byte_10_out_12),
    .out_13(byte_10_out_13), .out_14(byte_10_out_14), .Read_write(and_37_out), .in_7(in_11), .in_8(in_12),
    .in_9(in_13), .in_10(in_14), .out_15(byte_10_out_15), .out_16(byte_10_out_16), .out_17(byte_10_out_17),
    .out_18(byte_10_out_18), .in_2(CLEAR));
  Read_Stopper read_stopper_10 (
    .in_2(byte_10_out_11), .in_3(byte_10_out_12), .in_4(byte_10_out_13), .in_5(byte_10_out_14),
    .out_10(read_stopper_10_out_10), .out_11(read_stopper_10_out_11), .out_12(read_stopper_10_out_12),
    .out_13(read_stopper_10_out_13), .in_6(byte_10_out_15), .in_7(byte_10_out_16), .in_8(byte_10_out_17),
    .in_9(byte_10_out_18), .out_14(read_stopper_10_out_14), .out_15(read_stopper_10_out_15),
    .out_16(read_stopper_10_out_16), .out_17(read_stopper_10_out_17), .in_1(and_36_out));
  and and_38 (and_38_out, and_11_out, 1'b1);
  and and_39 (and_39_out, and_11_out, and_17_out);
  Byte byte_11 (
    .in_6(in_10), .in_5(in_9), .in_4(in_8), .in_3(in_7), .out_11(byte_11_out_11), .out_12(byte_11_out_12),
    .out_13(byte_11_out_13), .out_14(byte_11_out_14), .Read_write(and_39_out), .in_7(in_11), .in_8(in_12),
    .in_9(in_13), .in_10(in_14), .out_15(byte_11_out_15), .out_16(byte_11_out_16), .out_17(byte_11_out_17),
    .out_18(byte_11_out_18), .in_2(CLEAR));
  Read_Stopper read_stopper_11 (
    .in_2(byte_11_out_11), .in_3(byte_11_out_12), .in_4(byte_11_out_13), .in_5(byte_11_out_14),
    .out_10(read_stopper_11_out_10), .out_11(read_stopper_11_out_11), .out_12(read_stopper_11_out_12),
    .out_13(read_stopper_11_out_13), .in_6(byte_11_out_15), .in_7(byte_11_out_16), .in_8(byte_11_out_17),
    .in_9(byte_11_out_18), .out_14(read_stopper_11_out_14), .out_15(read_stopper_11_out_15),
    .out_16(read_stopper_11_out_16), .out_17(read_stopper_11_out_17), .in_1(and_38_out));
  and and_40 (and_40_out, and_12_out, 1'b1);
  and and_41 (and_41_out, and_12_out, and_17_out);
  Byte byte_12 (
    .in_6(in_10), .in_5(in_9), .in_4(in_8), .in_3(in_7), .out_11(byte_12_out_11), .out_12(byte_12_out_12),
    .out_13(byte_12_out_13), .out_14(byte_12_out_14), .Read_write(and_41_out), .in_7(in_11), .in_8(in_12),
    .in_9(in_13), .in_10(in_14), .out_15(byte_12_out_15), .out_16(byte_12_out_16), .out_17(byte_12_out_17),
    .out_18(byte_12_out_18), .in_2(CLEAR));
  Read_Stopper read_stopper_12 (
    .in_2(byte_12_out_11), .in_3(byte_12_out_12), .in_4(byte_12_out_13), .in_5(byte_12_out_14),
    .out_10(read_stopper_12_out_10), .out_11(read_stopper_12_out_11), .out_12(read_stopper_12_out_12),
    .out_13(read_stopper_12_out_13), .in_6(byte_12_out_15), .in_7(byte_12_out_16), .in_8(byte_12_out_17),
    .in_9(byte_12_out_18), .out_14(read_stopper_12_out_14), .out_15(read_stopper_12_out_15),
    .out_16(read_stopper_12_out_16), .out_17(read_stopper_12_out_17), .in_1(and_40_out));
  and and_42 (and_42_out, and_13_out, 1'b1);
  and and_43 (and_43_out, and_13_out, and_17_out);
  Byte byte_13 (
    .in_6(in_10), .in_5(in_9), .in_4(in_8), .in_3(in_7), .out_11(byte_13_out_11), .out_12(byte_13_out_12),
    .out_13(byte_13_out_13), .out_14(byte_13_out_14), .Read_write(and_43_out), .in_7(in_11), .in_8(in_12),
    .in_9(in_13), .in_10(in_14), .out_15(byte_13_out_15), .out_16(byte_13_out_16), .out_17(byte_13_out_17),
    .out_18(byte_13_out_18), .in_2(CLEAR));
  Read_Stopper read_stopper_13 (
    .in_2(byte_13_out_11), .in_3(byte_13_out_12), .in_4(byte_13_out_13), .in_5(byte_13_out_14),
    .out_10(read_stopper_13_out_10), .out_11(read_stopper_13_out_11), .out_12(read_stopper_13_out_12),
    .out_13(read_stopper_13_out_13), .in_6(byte_13_out_15), .in_7(byte_13_out_16), .in_8(byte_13_out_17),
    .in_9(byte_13_out_18), .out_14(read_stopper_13_out_14), .out_15(read_stopper_13_out_15),
    .out_16(read_stopper_13_out_16), .out_17(read_stopper_13_out_17), .in_1(and_42_out));
  and and_44 (and_44_out, and_14_out, 1'b1);
  and and_45 (and_45_out, and_14_out, and_17_out);
  Byte byte_14 (
    .in_6(in_10), .in_5(in_9), .in_4(in_8), .in_3(in_7), .out_11(byte_14_out_11), .out_12(byte_14_out_12),
    .out_13(byte_14_out_13), .out_14(byte_14_out_14), .Read_write(and_45_out), .in_7(in_11), .in_8(in_12),
    .in_9(in_13), .in_10(in_14), .out_15(byte_14_out_15), .out_16(byte_14_out_16), .out_17(byte_14_out_17),
    .out_18(byte_14_out_18), .in_2(CLEAR));
  Read_Stopper read_stopper_14 (
    .in_2(byte_14_out_11), .in_3(byte_14_out_12), .in_4(byte_14_out_13), .in_5(byte_14_out_14),
    .out_10(read_stopper_14_out_10), .out_11(read_stopper_14_out_11), .out_12(read_stopper_14_out_12),
    .out_13(read_stopper_14_out_13), .in_6(byte_14_out_15), .in_7(byte_14_out_16), .in_8(byte_14_out_17),
    .in_9(byte_14_out_18), .out_14(read_stopper_14_out_14), .out_15(read_stopper_14_out_15),
    .out_16(read_stopper_14_out_16), .out_17(read_stopper_14_out_17), .in_1(and_44_out));
  and and_46 (and_46_out, and_15_out, 1'b1);
  and and_47 (and_47_out, and_15_out, and_17_out);
  Byte byte_15 (
    .in_6(in_10), .in_5(in_9), .in_4(in_8), .in_3(in_7), .out_11(byte_15_out_11), .out_12(byte_15_out_12),
    .out_13(byte_15_out_13), .out_14(byte_15_out_14), .Read_write(and_47_out), .in_7(in_11), .in_8(in_12),
    .in_9(in_13), .in_10(in_14), .out_15(byte_15_out_15), .out_16(byte_15_out_16), .out_17(byte_15_out_17),
    .out_18(byte_15_out_18), .in_2(CLEAR));
  Read_Stopper read_stopper_15 (
    .in_2(byte_15_out_11), .in_3(byte_15_out_12), .in_4(byte_15_out_13), .in_5(byte_15_out_14),
    .out_10(read_stopper_15_out_10), .out_11(read_stopper_15_out_11), .out_12(read_stopper_15_out_12),
    .out_13(read_stopper_15_out_13), .in_6(byte_15_out_15), .in_7(byte_15_out_16), .in_8(byte_15_out_17),
    .in_9(byte_15_out_18), .out_14(read_stopper_15_out_14), .out_15(read_stopper_15_out_15),
    .out_16(read_stopper_15_out_16), .out_17(read_stopper_15_out_17), .in_1(and_46_out));
  and and_48 (and_48_out, and_16_out, 1'b1);
  and and_49 (and_49_out, and_16_out, and_17_out);
  Byte byte_16 (
    .in_6(in_10), .in_5(in_9), .in_4(in_8), .in_3(in_7), .out_11(byte_16_out_11), .out_12(byte_16_out_12),
    .out_13(byte_16_out_13), .out_14(byte_16_out_14), .Read_write(and_49_out), .in_7(in_11), .in_8(in_12),
    .in_9(in_13), .in_10(in_14), .out_15(byte_16_out_15), .out_16(byte_16_out_16), .out_17(byte_16_out_17),
    .out_18(byte_16_out_18), .in_2(CLEAR));
  Read_Stopper read_stopper_16 (
    .in_2(byte_16_out_11), .in_3(byte_16_out_12), .in_4(byte_16_out_13), .in_5(byte_16_out_14),
    .out_10(read_stopper_16_out_10), .out_11(read_stopper_16_out_11), .out_12(read_stopper_16_out_12),
    .out_13(read_stopper_16_out_13), .in_6(byte_16_out_15), .in_7(byte_16_out_16), .in_8(byte_16_out_17),
    .in_9(byte_16_out_18), .out_14(read_stopper_16_out_14), .out_15(read_stopper_16_out_15),
    .out_16(read_stopper_16_out_16), .out_17(read_stopper_16_out_17), .in_1(and_48_out));
  or or_1 (out_16, read_stopper_1_out_10, read_stopper_2_out_10, read_stopper_3_out_10, read_stopper_4_out_10, read_stopper_5_out_10, read_stopper_6_out_10, read_stopper_7_out_10, read_stopper_8_out_10, read_stopper_9_out_10, read_stopper_10_out_10, read_stopper_11_out_10, read_stopper_12_out_10, read_stopper_13_out_10, read_stopper_14_out_10, read_stopper_15_out_10, read_stopper_16_out_10);
  or or_2 (out_17, read_stopper_1_out_11, read_stopper_2_out_11, read_stopper_3_out_11, read_stopper_4_out_11, read_stopper_5_out_11, read_stopper_6_out_11, read_stopper_7_out_11, read_stopper_8_out_11, read_stopper_9_out_11, read_stopper_10_out_11, read_stopper_11_out_11, read_stopper_12_out_11, read_stopper_13_out_11, read_stopper_14_out_11, read_stopper_15_out_11, read_stopper_16_out_11);
  or or_3 (out_18, read_stopper_1_out_12, read_stopper_2_out_12, read_stopper_3_out_12, read_stopper_15_out_12, read_stopper_16_out_12, read_stopper_4_out_12, read_stopper_5_out_12, read_stopper_6_out_12, read_stopper_7_out_12, read_stopper_8_out_12, read_stopper_9_out_12, read_stopper_10_out_12, read_stopper_11_out_12, read_stopper_12_out_12, read_stopper_13_out_12, read_stopper_14_out_12);
  or or_4 (out_19, read_stopper_1_out_13, read_stopper_2_out_13, read_stopper_3_out_13, read_stopper_4_out_13, read_stopper_5_out_13, read_stopper_6_out_13, read_stopper_14_out_13, read_stopper_7_out_13, read_stopper_8_out_13, read_stopper_9_out_13, read_stopper_10_out_13, read_stopper_11_out_13, read_stopper_12_out_13, read_stopper_13_out_13, read_stopper_15_out_13, read_stopper_16_out_13);
  or or_5 (out_20, read_stopper_1_out_14, read_stopper_2_out_14, read_stopper_3_out_14, read_stopper_4_out_14, read_stopper_5_out_14, read_stopper_6_out_14, read_stopper_7_out_14, read_stopper_8_out_14, read_stopper_9_out_14, read_stopper_10_out_14, read_stopper_11_out_14, read_stopper_12_out_14, read_stopper_13_out_14, read_stopper_14_out_14, read_stopper_15_out_14, read_stopper_16_out_14);
  or or_6 (out_21, read_stopper_1_out_15, read_stopper_2_out_15, read_stopper_3_out_15, read_stopper_4_out_15, read_stopper_5_out_15, read_stopper_6_out_15, read_stopper_7_out_15, read_stopper_8_out_15, read_stopper_9_out_15, read_stopper_10_out_15, read_stopper_11_out_15, read_stopper_12_out_15, read_stopper_13_out_15, read_stopper_14_out_15, read_stopper_15_out_15, read_stopper_16_out_15);
  or or_7 (out_22, read_stopper_1_out_16, read_stopper_2_out_16, read_stopper_3_out_16, read_stopper_4_out_16, read_stopper_5_out_16, read_stopper_6_out_16, read_stopper_7_out_16, read_stopper_8_out_16, read_stopper_9_out_16, read_stopper_10_out_16, read_stopper_11_out_16, read_stopper_12_out_16, read_stopper_13_out_16, read_stopper_14_out_16, read_stopper_15_out_16, read_stopper_16_out_16);
  or or_8 (out_23, read_stopper_1_out_17, read_stopper_2_out_17, read_stopper_3_out_17, read_stopper_4_out_17, read_stopper_5_out_17, read_stopper_6_out_17, read_stopper_7_out_17, read_stopper_8_out_17, read_stopper_9_out_17, read_stopper_10_out_17, read_stopper_11_out_17, read_stopper_12_out_17, read_stopper_13_out_17, read_stopper_14_out_17, read_stopper_15_out_17, read_stopper_16_out_17);
endmodule

module Read_Stopper (
  input  in_1,
  input  in_2,
  input  in_3,
  input  in_4,
  input  in_5,
  input  in_6,
  input  in_7,
  input  in_8,
  input  in_9,
  output out_10,
  output out_11,
  output out_12,
  output out_13,
  output out_14,
  output out_15,
  output out_16,
  output out_17
);

  and and_1 (out_10, in_1, in_2);
  and and_2 (out_11, in_1, in_3);
  and and_3 (out_12, in_1, in_4);
  and and_4 (out_13, in_1, in_5);
  and and_5 (out_14, in_6, in_1);
  and and_6 (out_15, in_7, in_1);
  and and_7 (out_16, in_8, in_1);
  and and_8 (out_17, in_9, in_1);
endmodule

module Computer (
  input  in_1,
  input  in_2,
  input  in_3,
  input  in_4,
  input  in_5,
  input  in_6,
  input  in_7,
  input  in_8,
  input  in_9,
  input  in_10,
  input  in_11,
  input  in_12,
  input  in_13,
  input  in_14,
  input  in_15
);

  RAM ram_1 (
    .Clock(in_1), .Read_Write(in_3), .Address(in_6), .in_6(in_7), .in_7(in_8), .in_8(in_9), .in_9(in_10),
    .in_10(in_11), .in_11(in_12), .in_12(in_13), .in_13(in_14), .in_14(in_15), .in_4(in_5), .in_3(in_4),
    .CLEAR(in_2));  // open: out_16, out_17, out_18, out_19, out_20, out_21, out_22, out_23
endmodule
