// Logisim project 8bitTo3dec.circ as structural Verilog: 1 circuit, main circuit main
module main (
  input  [7:0] in_1,
  output out_2,
  output out_3,
  output out_4,
  output out_5,
  output out_6,
  output out_7,
  output out_8,
  output out_9,
  output out_10,
  output out_11,
  output out_12,
  output out_13,
  output out_14,
  output out_15,
  output out_16,
  output out_17,
  output out_18,
  output out_19,
  output out_20,
  output out_21,
  output out_22
);

  wire c1_out_5, c1_out_6, c1_out_7, c1_out_8, c2_out_5, c2_out_6, c2_out_7, c2_out_8, c3_out_5, c3_out_6,
       c3_out_7, c3_out_8, c4_out_5, c4_out_6, c4_out_7, c4_out_8, c5_out_5, c5_out_6, c5_out_7, c5_out_8,
       c6_out_5, c6_out_6, c6_out_7, c6_out_8, c7_out_5, c7_out_6, c7_out_7, c7_out_8, undriven, undriven_2;

  // Probe on c6_out_5
  bcd_decoder_main main_1 (
    .A(c7_out_5), .B(c6_out_5), .C(1'b0), .D(1'b0), .a_2(out_2), .b_2(out_5), .c_2(out_8), .d_2(out_11),
    .e(out_14), .f(out_18), .g(out_17));  // open: BLANKING
  // Probe on c7_out_5
  shift3_display_main c6 (
    .in_1(1'b0), .in_2(c1_out_5), .in_3(c2_out_5), .in_4(c3_out_5), .out_5(c6_out_5), .out_6(c6_out_6),
    .out_7(c6_out_7), .out_8(c6_out_8));
  // Probe on c7_out_6
  shift3_display_main c7 (
    .in_1(c6_out_6), .in_2(c6_out_7), .in_3(c6_out_8), .in_4(c4_out_5), .out_5(c7_out_5), .out_6(c7_out_6),
    .out_7(c7_out_7), .out_8(c7_out_8));
  // Probe on c7_out_7
  // Probe on c7_out_8
  bcd_decoder_main main_2 (
    .A(c5_out_5), .B(c7_out_8), .C(c7_out_7), .D(c7_out_6), .BLANKING(undriven), .a_2(out_3), .b_2(out_6),
    .c_2(out_9), .d_2(out_12), .e(out_15), .f(out_20), .g(out_19));
  shift3_display_main c1 (
    .in_1(1'b0), .in_2(in_1[7]), .in_3(in_1[6]), .in_4(in_1[5]), .out_5(c1_out_5), .out_6(c1_out_6),
    .out_7(c1_out_7), .out_8(c1_out_8));
  shift3_display_main c2 (
    .in_1(c1_out_6), .in_2(c1_out_7), .in_3(c1_out_8), .in_4(in_1[4]), .out_5(c2_out_5), .out_6(c2_out_6),
    .out_7(c2_out_7), .out_8(c2_out_8));
  // Probe on c5_out_5
  shift3_display_main c3 (
    .in_1(c2_out_6), .in_2(c2_out_7), .in_3(c2_out_8), .in_4(in_1[3]), .out_5(c3_out_5), .out_6(c3_out_6),
    .out_7(c3_out_7), .out_8(c3_out_8));
  // Probe on c5_out_6
  shift3_display_main c4 (
    .in_1(c3_out_6), .in_2(c3_out_7), .in_3(c3_out_8), .in_4(in_1[2]), .out_5(c4_out_5), .out_6(c4_out_6),
    .out_7(c4_out_7), .out_8(c4_out_8));
  // Probe on c5_out_7
  shift3_display_main c5 (
    .in_1(c4_out_6), .in_2(c4_out_7), .in_3(c4_out_8), .in_4(in_1[1]), .out_5(c5_out_5), .out_6(c5_out_6),
    .out_7(c5_out_7), .out_8(c5_out_8));
  // Probe on c5_out_8
  bcd_decoder_main main_3 (
    .A(in_1[0]), .B(c5_out_8), .C(c5_out_7), .D(c5_out_6), .BLANKING(undriven_2), .a_2(out_4), .b_2(out_7),
    .c_2(out_10), .d_2(out_13), .e(out_16), .f(out_22), .g(out_21));
  // Probe on in_1[0]

  // Notes on the sheet:
  //   enable
  //   {           Huns           }
  //   outpu
  //   input
  //   {                              tens                }
  //   {                  Units               }
endmodule
