// Logisim project CPU.circ as structural Verilog: 1 circuit, main circuit main
module main (
  input  [7:0] Data_RAM,
  input  ON
);

  wire clock_1_out, CU_add_alu, CU_ir__mbr, CU_mar____ir_address, CU_mar__pc__pc_plus_plus, CU_mbr____r0,
       CU_mbr____r1, CU_mbr__m_mar, CU_pc__ir_address____br_eq, CU_pc__ir_address____br_n_eq,
       CU_substract_alu, not_1_out, not_2_out, not_3_out, not_4_out, not_5_out, not_6_out, or_3_out,
       or_4_out, or_5_out, or_6_out, or_7_out, or_8_out;
  wire [1:0] or_2_out;
  wire [3:0] IR_output, IR_output_2, multiplexer_2_out, PC_out_5;
  wire [7:0] MBR_output, multiplexer_1_out, R1_output, R2_output;

  Clock #(.highDuration(3), .lowDuration(3)) clock_1 (.out(clock_1_out));
  or or_1 (or_2_out[1], CU_mar____ir_address, not_2_out, not_1_out);
  not not_1 (not_1_out, CU_mbr____r0);
  not not_2 (not_2_out, CU_mbr____r1);
  Multiplexer #(.select(2), .width(8), .enable("false")) multiplexer_1 (
    .in0(R1_output), .in1(R2_output), .in2(Data_RAM), .out(multiplexer_1_out), .sel(or_2_out));  // open: in3
  or or_2 (or_2_out[0], not_4_out, CU_mbr____r1, not_3_out);
  not not_3 (not_3_out, CU_mbr____r0);
  not not_4 (not_4_out, CU_mar____ir_address);
  or or_3 (or_3_out, CU_mbr____r0, CU_mbr__m_mar, CU_mbr____r1);
  Multiplexer #(.width(4), .enable("false")) multiplexer_2 (
    .in0(PC_out_5), .in1(IR_output_2), .out(multiplexer_2_out), .sel(not_5_out));
  not not_5 (not_5_out, CU_mar__pc__pc_plus_plus);
  or or_4 (or_4_out, CU_mar__pc__pc_plus_plus, CU_mar____ir_address);
  _4_bit_register__MAR MAR (.Clock(clock_1_out), .R_0__W_1(or_4_out), .Input(multiplexer_2_out));  // open: Output
  Register MBR (.Clock(clock_1_out), .R_0__W_1(or_3_out), .Input(multiplexer_1_out), .Output(MBR_output));
  CU CU (
    .Clock(clock_1_out), .OP_code(IR_output), .MAR__Pc__PC_plus_plus(CU_mar__pc__pc_plus_plus),
    .IR__MBR(CU_ir__mbr), .Start(ON), .MBR__M_MAR(CU_mbr__m_mar), .MAR____IR_address(CU_mar____ir_address),
    .MBR____R0(CU_mbr____r0), .MBR____R1(CU_mbr____r1), .ADD_alu(CU_add_alu),
    .Substract_alu(CU_substract_alu), .PC__IR_address____br_eq(CU_pc__ir_address____br_eq),
    .PC__IR_address____br_n_eq(CU_pc__ir_address____br_n_eq));  // open: Compare_alu, A_B_alu_____registers
  Register IR (.Clock(clock_1_out), .R_0__W_1(CU_ir__mbr), .Input(MBR_output), .Output({IR_output, IR_output_2}));
  or or_5 (or_5_out, CU_pc__ir_address____br_eq, CU_pc__ir_address____br_n_eq, CU_mar__pc__pc_plus_plus);
  or or_6 (or_6_out, CU_pc__ir_address____br_n_eq, CU_pc__ir_address____br_eq);
  programcounter__alec_main PC (
    .Clock(clock_1_out), .Activate(or_5_out), .INC_0__SET_1(or_6_out), .in_4(IR_output_2), .out_5(PC_out_5));
  Register R1 (.Clock(clock_1_out), .Output(R1_output));  // open: R_0__W_1, Input
  Register R2 (.Clock(clock_1_out), .Output(R2_output));  // open: R_0__W_1, Input
  not not_6 (not_6_out, CU_add_alu);
  or or_7 (or_7_out, not_6_out, CU_substract_alu);
  or or_8 (or_8_out, CU_add_alu, CU_substract_alu);
  Register L (.Input(R1_output));  // open: Clock, R_0__W_1, Output
  alu_main ALU (.Control0(or_7_out), .Control1(or_8_out));  // open: A, B, Result, Zero, Carry, Overflow, Negative
  Register R (.Input(R2_output));  // open: Clock, R_0__W_1, Output
endmodule
