// Logisim project Control Unit.circ as structural Verilog: 23 circuits, main circuit Counter
module Counter (
  input  Clock,
  input  Start,
  output [7:0] out_3
);

  wire and_1_out, j_k_ff_2_qn, j_k_ff_3_qn;
  wire [2:0] j_k_ff_3_q;

  J_K_Flip_Flop j_k_ff_1 (.J(1'b1), .clk(j_k_ff_2_qn), .K(1'b1), .Q(j_k_ff_3_q[2]));  // open: Qn, preset, en, reset
  Decoder #(.select(3)) decoder_1 (
    .out0(out_3[7]), .out1(out_3[6]), .out2(out_3[5]), .out3(out_3[4]), .out4(out_3[3]), .out5(out_3[2]),
    .out6(out_3[1]), .out7(out_3[0]), .sel(j_k_ff_3_q));  // open: en
  J_K_Flip_Flop j_k_ff_2 (
    .J(1'b1), .clk(j_k_ff_3_qn), .K(1'b1), .Q(j_k_ff_3_q[1]), .Qn(j_k_ff_2_qn));  // open: preset, en, reset
  J_K_Flip_Flop j_k_ff_3 (
    .J(1'b1), .clk(and_1_out), .K(1'b1), .Q(j_k_ff_3_q[0]), .Qn(j_k_ff_3_qn));  // open: preset, en, reset
  and and_1 (and_1_out, Clock, Start);
endmodule

module MBR____M_MAR (
  input  [3:0] OP,
  output out_2
);

  wire and_1_out, and_2_out, not_1_out, not_2_out, not_3_out, not_4_out;

  not not_1 (not_1_out, OP[1]);
  not not_2 (not_2_out, OP[3]);
  not not_3 (not_3_out, OP[2]);
  and and_1 (and_1_out, not_2_out, not_3_out, not_1_out, OP[0]);
  or or_1 (out_2, and_1_out, and_2_out);
  not not_4 (not_4_out, OP[0]);
  and and_2 (and_2_out, not_2_out, not_3_out, OP[1], not_4_out);
endmodule

module MAR____IR_address (
  input  [3:0] OP,
  output out_2
);

  wire and_1_out, and_2_out, and_3_out, and_4_out, not_1_out, not_2_out, not_3_out, not_4_out;

  not not_1 (not_1_out, OP[1]);
  not not_2 (not_2_out, OP[3]);
  not not_3 (not_3_out, OP[2]);
  and and_1 (and_1_out, not_2_out, not_3_out, not_1_out, OP[0]);
  not not_4 (not_4_out, OP[0]);
  and and_2 (and_2_out, not_2_out, not_3_out, OP[1], not_4_out);
  or or_1 (out_2, and_1_out, and_2_out, and_4_out, and_3_out);
  and and_3 (and_3_out, not_2_out, OP[2], not_1_out, not_4_out);
  and and_4 (and_4_out, not_2_out, not_3_out, OP[1], OP[0]);
endmodule

module MBR____R0 (
  input  [3:0] OP,
  output out_2
);

  wire not_1_out, not_2_out;

  not not_1 (not_1_out, OP[3]);
  not not_2 (not_2_out, OP[2]);
  and and_1 (out_2, not_1_out, not_2_out, OP[1], OP[0]);
endmodule

module MBR____R1 (
  input  [3:0] OP,
  output out_2
);

  wire not_1_out, not_2_out, not_3_out;

  not not_1 (not_1_out, OP[3]);
  not not_2 (not_2_out, OP[0]);
  not not_3 (not_3_out, OP[1]);
  and and_1 (out_2, not_1_out, OP[2], not_3_out, not_2_out);
endmodule

module M_MAR___MBR (
  input  [3:0] OP,
  output out_2
);

  wire and_1_out, and_2_out, not_1_out, not_2_out, not_3_out, not_4_out;

  not not_1 (not_1_out, OP[3]);
  not not_2 (not_2_out, OP[2]);
  and and_1 (and_1_out, not_1_out, not_2_out, OP[1], OP[0]);
  or or_1 (out_2, and_1_out, and_2_out);
  not not_3 (not_3_out, OP[0]);
  not not_4 (not_4_out, OP[1]);
  and and_2 (and_2_out, not_1_out, OP[2], not_4_out, not_3_out);
endmodule

module R0____MBR (
  input  [3:0] OP,
  output out_2
);

  wire not_1_out, not_2_out, not_3_out;

  not not_1 (not_1_out, OP[2]);
  not not_2 (not_2_out, OP[1]);
  not not_3 (not_3_out, OP[3]);
  and and_1 (out_2, not_3_out, not_1_out, not_2_out, OP[0]);
endmodule

module R1____MBR (
  input  [3:0] OP,
  output out_2
);

  wire not_1_out, not_2_out, not_3_out;

  not not_1 (not_1_out, OP[0]);
  not not_2 (not_2_out, OP[3]);
  not not_3 (not_3_out, OP[2]);
  and and_1 (out_2, not_2_out, not_3_out, OP[1], not_1_out);
endmodule

module A_B_alu____registers (
  input  [3:0] OP,
  output out_2
);

  wire and_1_out, and_2_out, and_3_out, and_4_out, not_1_out, not_2_out, not_3_out, not_4_out;

  not not_1 (not_1_out, OP[3]);
  not not_2 (not_2_out, OP[1]);
  and and_1 (and_1_out, not_1_out, OP[2], not_2_out, OP[0]);
  not not_3 (not_3_out, OP[0]);
  and and_2 (and_2_out, not_1_out, OP[2], OP[1], not_3_out);
  or or_1 (out_2, and_1_out, and_2_out, and_3_out, and_4_out);
  not not_4 (not_4_out, OP[2]);
  and and_3 (and_3_out, not_1_out, OP[2], OP[1], OP[0]);
  and and_4 (and_4_out, OP[3], not_4_out, not_2_out, not_3_out);
endmodule

module Add_ALU (
  input  [3:0] OP,
  output out_2
);

  wire not_1_out, not_2_out;

  not not_1 (not_1_out, OP[1]);
  not not_2 (not_2_out, OP[3]);
  and and_1 (out_2, not_2_out, OP[2], not_1_out, OP[0]);
endmodule

module SUB_ALU (
  input  [3:0] OP,
  output out_2
);

  wire not_1_out, not_2_out;

  not not_1 (not_1_out, OP[0]);
  not not_2 (not_2_out, OP[3]);
  and and_1 (out_2, not_2_out, OP[2], OP[1], not_1_out);
endmodule

module PC____IR_Address____br_eq (
  input  [3:0] OP,
  output out_2
);

  wire not_1_out;

  not not_1 (not_1_out, OP[3]);
  and and_1 (out_2, not_1_out, OP[2], OP[1], OP[0]);
endmodule

module PC____IR_Address____br_n_eq (
  input  [3:0] OP,
  output out_2
);

  wire not_1_out, not_2_out, not_3_out;

  not not_1 (not_1_out, OP[1]);
  not not_2 (not_2_out, OP[2]);
  not not_3 (not_3_out, OP[0]);
  and and_1 (out_2, OP[3], not_2_out, not_1_out, not_3_out);
endmodule

module CU (
  input  Clock,
  input  [3:0] OP_code,
  input  Start,
  input  STOP_SWICH,
  output MAR__Pc__PC_plus_plus,
  output IR__MBR,
  output MBR__M_MAR,
  output MAR____IR_address,
  output MBR____R0,
  output MBR____R1,
  output M_MAR_____MBR,
  output ADD_alu,
  output Substract_alu,
  output R0____MBR,
  output R1____MBR,
  output A_B_alu_____registers,
  output R1____ALU_result,
  output PC__IR_address____br_eq,
  output PC__IR_address____br_n_eq,
  output RAM_1111_____MBR,
  output Display____RAM_1111,
  output RAM_1111_____Display,
  output MBR____RAM_1111,
  output Multiply,
  output R____Multiply_result,
  output Br_eq_set,
  output Br_n_eq_set,
  output out_28
);

  wire a_b_alu_registers_1_out_2, add_alu_1_out_2, and_1_out, and_2_out, and_4_out, and_5_out, and_9_out,
       and_10_out, and_18_out, and_19_out, and_21_out, and_22_out, and_27_out, and_28_out, input_1_out_2,
       m_mar_mbr_1_out_2, MAR__IR_address_out_2, MBR__M_MAR_out_2, mbr_r0_1_out_2, mbr_r0_input_1_out_2,
       mbr_r1_1_out_2, mbr_r1_input_1_out_2, mult_1_out_2, not_1_out, pc_ir_address_br_eq_1_out_2,
       pc_ir_address_br_n_eq_1_out_2, print_1_out_2, r0_mbr_1_out_2, r0_mbr_print_1_out_2, r1_alu_1_out_2,
       r1_mbr_1_out_2, r1_mbr_print_1_out_2, stop_1_out_2, sub_alu_1_out_2;
  wire [7:0] counter_1_out_3;

  Stop stop_1 (.OP(OP_code), .out_2(stop_1_out_2));
  MBR____M_MAR u_MBR__M_MAR (.OP(OP_code), .out_2(MBR__M_MAR_out_2));
  MAR____IR_address MAR__IR_address (.OP(OP_code), .out_2(MAR__IR_address_out_2));
  MBR____R0 mbr_r0_1 (.OP(OP_code), .out_2(mbr_r0_1_out_2));
  MBR____R1 mbr_r1_1 (.OP(OP_code), .out_2(mbr_r1_1_out_2));
  M_MAR___MBR m_mar_mbr_1 (.OP(OP_code), .out_2(m_mar_mbr_1_out_2));
  R0____MBR r0_mbr_1 (.OP(OP_code), .out_2(r0_mbr_1_out_2));
  R1____MBR r1_mbr_1 (.OP(OP_code), .out_2(r1_mbr_1_out_2));
  A_B_alu____registers a_b_alu_registers_1 (.OP(OP_code), .out_2(a_b_alu_registers_1_out_2));
  Add_ALU add_alu_1 (.OP(OP_code), .out_2(add_alu_1_out_2));
  SUB_ALU sub_alu_1 (.OP(OP_code), .out_2(sub_alu_1_out_2));
  R1____ALU r1_alu_1 (.OP(OP_code), .out_2(r1_alu_1_out_2));
  PC____IR_Address____br_eq pc_ir_address_br_eq_1 (.OP(OP_code), .out_2(pc_ir_address_br_eq_1_out_2));
  PC____IR_Address____br_n_eq pc_ir_address_br_n_eq_1 (.OP(OP_code), .out_2(pc_ir_address_br_n_eq_1_out_2));
  Print print_1 (.OP(OP_code), .out_2(print_1_out_2));
  R0____MBR_print r0_mbr_print_1 (.OP(OP_code), .out_2(r0_mbr_print_1_out_2));
  R1____MBR_print r1_mbr_print_1 (.OP(OP_code), .out_2(r1_mbr_print_1_out_2));
  MBR___R0_input mbr_r0_input_1 (.OP(OP_code), .out_2(mbr_r0_input_1_out_2));
  MBR___R1_input mbr_r1_input_1 (.OP(OP_code), .out_2(mbr_r1_input_1_out_2));
  Input input_1 (.OP(OP_code), .out_2(input_1_out_2));
  MULT mult_1 (.OP(OP_code), .out_2(mult_1_out_2));
  Counter counter_1 (
    .out_3({counter_1_out_3[7], MAR__Pc__PC_plus_plus, counter_1_out_3[5], IR__MBR, counter_1_out_3[3:0]}),
    .Clock(Clock), .Start(and_1_out));
  and and_1 (and_1_out, not_1_out, Start);
  and and_2 (and_2_out, counter_1_out_3[2], MBR__M_MAR_out_2);
  and and_3 (MAR____IR_address, counter_1_out_3[3], MAR__IR_address_out_2);
  and and_4 (and_4_out, counter_1_out_3[2], mbr_r0_1_out_2);
  and and_5 (and_5_out, counter_1_out_3[2], mbr_r1_1_out_2);
  and and_6 (M_MAR_____MBR, counter_1_out_3[1], m_mar_mbr_1_out_2);
  and and_7 (ADD_alu, counter_1_out_3[2], add_alu_1_out_2);
  and and_8 (Substract_alu, counter_1_out_3[2], sub_alu_1_out_2);
  and and_9 (and_9_out, counter_1_out_3[1], r0_mbr_1_out_2);
  and and_10 (and_10_out, counter_1_out_3[1], r1_mbr_1_out_2);
  and and_11 (A_B_alu_____registers, a_b_alu_registers_1_out_2, counter_1_out_3[3]);
  and and_12 (R1____ALU_result, counter_1_out_3[1], r1_alu_1_out_2);
  and and_13 (PC__IR_address____br_eq, counter_1_out_3[1], pc_ir_address_br_eq_1_out_2);
  and and_14 (PC__IR_address____br_n_eq, counter_1_out_3[1], pc_ir_address_br_n_eq_1_out_2);
  and and_15 (RAM_1111_____MBR, counter_1_out_3[2], print_1_out_2);
  and and_16 (RAM_1111_____Display, counter_1_out_3[3], input_1_out_2);
  and and_17 (Multiply, counter_1_out_3[3], mult_1_out_2);
  not not_1 (not_1_out, stop_1_out_2);
  and and_18 (and_18_out, counter_1_out_3[3], r0_mbr_print_1_out_2);
  and and_19 (and_19_out, counter_1_out_3[3], r1_mbr_print_1_out_2);
  and and_20 (MBR____RAM_1111, counter_1_out_3[2], input_1_out_2);
  and and_21 (and_21_out, mbr_r0_input_1_out_2, counter_1_out_3[1]);
  and and_22 (and_22_out, counter_1_out_3[1], mbr_r1_input_1_out_2);
  and and_23 (Display____RAM_1111, counter_1_out_3[1], print_1_out_2);
  and and_24 (R____Multiply_result, counter_1_out_3[0], mult_1_out_2);
  and and_25 (Br_eq_set, counter_1_out_3[0], pc_ir_address_br_eq_1_out_2);
  and and_26 (Br_n_eq_set, counter_1_out_3[0], pc_ir_address_br_n_eq_1_out_2);
  or or_1 (R1____MBR, and_10_out, and_22_out);
  and and_27 (and_27_out, A_B_alu_____registers, pc_ir_address_br_eq_1_out_2);
  and and_28 (and_28_out, A_B_alu_____registers, pc_ir_address_br_n_eq_1_out_2);
  or or_2 (MBR__M_MAR, counter_1_out_3[5], and_2_out);
  or or_3 (MBR____R0, and_4_out, and_18_out);
  or or_4 (MBR____R1, and_5_out, and_19_out);
  or or_5 (R0____MBR, and_9_out, and_21_out);
  or or_6 (out_28, and_27_out, and_28_out);
endmodule

module R1____ALU (
  input  [3:0] OP,
  output out_2
);

  wire and_1_out, and_2_out, not_1_out, not_2_out, not_3_out;

  not not_1 (not_1_out, OP[3]);
  not not_2 (not_2_out, OP[1]);
  and and_1 (and_1_out, not_1_out, OP[2], not_2_out, OP[0]);
  or or_1 (out_2, and_1_out, and_2_out);
  not not_3 (not_3_out, OP[0]);
  and and_2 (and_2_out, not_1_out, OP[2], OP[1], not_3_out);
endmodule

module Print (
  input  [3:0] OP,
  output out_2
);

  wire and_1_out, and_2_out, not_1_out, not_2_out, not_3_out;

  not not_1 (not_1_out, OP[2]);
  not not_2 (not_2_out, OP[1]);
  and and_1 (and_1_out, OP[3], not_1_out, not_2_out, OP[0]);
  or or_1 (out_2, and_1_out, and_2_out);
  not not_3 (not_3_out, OP[0]);
  and and_2 (and_2_out, OP[3], not_1_out, OP[1], not_3_out);
endmodule

module Input (
  input  [3:0] OP,
  output out_2
);

  wire and_1_out, and_2_out, not_1_out, not_2_out, not_3_out;

  not not_1 (not_1_out, OP[2]);
  and and_1 (and_1_out, OP[3], not_1_out, OP[1], OP[0]);
  or or_1 (out_2, and_1_out, and_2_out);
  not not_2 (not_2_out, OP[0]);
  not not_3 (not_3_out, OP[1]);
  and and_2 (and_2_out, OP[3], OP[2], not_3_out, not_2_out);
endmodule

module MULT (
  input  [3:0] OP,
  output out_2
);

  wire not_1_out;

  not not_1 (not_1_out, OP[0]);
  and and_1 (out_2, OP[3], OP[2], OP[1], not_1_out);
endmodule

module Stop (
  input  [3:0] OP,
  output out_2
);

  wire not_1_out;

  not not_1 (not_1_out, OP[1]);
  and and_1 (out_2, OP[3], OP[2], not_1_out, OP[0]);
endmodule

module R0____MBR_print (
  input  [3:0] OP,
  output out_2
);

  wire not_1_out, not_2_out;

  not not_1 (not_1_out, OP[1]);
  not not_2 (not_2_out, OP[2]);
  and and_1 (out_2, OP[3], not_2_out, not_1_out, OP[0]);
endmodule

module R1____MBR_print (
  input  [3:0] OP,
  output out_2
);

  wire not_1_out, not_2_out;

  not not_1 (not_1_out, OP[0]);
  not not_2 (not_2_out, OP[2]);
  and and_1 (out_2, OP[3], not_2_out, OP[1], not_1_out);
endmodule

module MBR___R0_input (
  input  [3:0] OP,
  output out_2
);

  wire not_1_out;

  not not_1 (not_1_out, OP[2]);
  and and_1 (out_2, OP[3], not_1_out, OP[1], OP[0]);
endmodule

module MBR___R1_input (
  input  [3:0] OP,
  output out_2
);

  wire not_1_out, not_2_out;

  not not_1 (not_1_out, OP[1]);
  not not_2 (not_2_out, OP[0]);
  and and_1 (out_2, OP[3], OP[2], not_1_out, not_2_out);
endmodule
