// Logisim project PC & Incrementer.circ as structural Verilog: 2 circuits, main circuit 4-bit PC & incrementer
module _4_bit_PC___incrementer (
  input  Clock,
  input  R_0__W_1,
  input  [3:0] Input,
  input  Incrementer,
  output [3:0] Output
);

  wire and_1_out, and_2_out, and_3_out, and_4_out, and_5_out, and_6_out, and_7_out, and_8_out, j_k_ff_1_q,
       j_k_ff_2_q, j_k_ff_3_q, j_k_ff_4_q, not_1_out, not_2_out, not_3_out, not_4_out, not_5_out;
  wire [3:0] and_9_out;

  not not_1 (not_1_out, R_0__W_1);
  not not_2 (not_2_out, Input[0]);
  not not_3 (not_3_out, Input[1]);
  not not_4 (not_4_out, Input[2]);
  not not_5 (not_5_out, Input[3]);
  and and_1 (and_1_out, R_0__W_1, Input[0]);
  and and_2 (and_2_out, R_0__W_1, not_2_out);
  and and_3 (and_3_out, R_0__W_1, Input[1]);
  and and_4 (and_4_out, R_0__W_1, not_3_out);
  and and_5 (and_5_out, R_0__W_1, Input[2]);
  and and_6 (and_6_out, R_0__W_1, not_4_out);
  and and_7 (and_7_out, R_0__W_1, Input[3]);
  and and_8 (and_8_out, R_0__W_1, not_5_out);
  J_K_Flip_Flop j_k_ff_1 (.J(and_1_out), .clk(Clock), .K(and_2_out), .Q(j_k_ff_1_q));  // open: Qn, preset, en, reset
  J_K_Flip_Flop j_k_ff_2 (.J(and_3_out), .clk(Clock), .K(and_4_out), .Q(j_k_ff_2_q));  // open: Qn, preset, en, reset
  J_K_Flip_Flop j_k_ff_3 (.J(and_5_out), .clk(Clock), .K(and_6_out), .Q(j_k_ff_3_q));  // open: Qn, preset, en, reset
  J_K_Flip_Flop j_k_ff_4 (.J(and_7_out), .clk(Clock), .K(and_8_out), .Q(j_k_ff_4_q));  // open: Qn, preset, en, reset
  and and_9 (and_9_out[0], not_1_out, j_k_ff_1_q);
  and and_10 (and_9_out[1], not_1_out, j_k_ff_2_q);
  and and_11 (and_9_out[2], not_1_out, j_k_ff_3_q);
  and and_12 (and_9_out[3], not_1_out, j_k_ff_4_q);
  Incrementer incrementer_1 (.out_4(Output), .Increment(Incrementer), .Input(and_9_out));  // open: Clock
endmodule

module Incrementer (
  input  Increment,
  input  Clock,
  input  [3:0] Input,
  output [3:0] out_4
);

  wire j_k_ff_3_qn, j_k_ff_4_qn, multiplexer_1_out, multiplexer_2_out, multiplexer_3_out, multiplexer_4_out,
       multiplexer_5_out, multiplexer_6_out, multiplexer_7_out, multiplexer_8_out, multiplexer_9_out,
       multiplexer_10_out, not_1_out, not_2_out, not_3_out, not_4_out, not_5_out, not_6_out;

  J_K_Flip_Flop j_k_ff_1 (
    .J(Input[3]), .clk(multiplexer_1_out), .K(not_1_out), .Q(out_4[3]));  // open: Qn, preset, en, reset
  not not_1 (not_1_out, Input[3]);
  not not_2 (not_2_out, 1'b1);
  Multiplexer #(.enable("false")) multiplexer_1 (
    .in0(not_2_out), .in1(Clock), .out(multiplexer_1_out), .sel(not_6_out));
  Multiplexer #(.enable("false")) multiplexer_2 (.in0(1'b1), .in1(not_3_out), .out(multiplexer_2_out), .sel(not_6_out));
  not not_3 (not_3_out, Input[2]);
  Multiplexer #(.enable("false")) multiplexer_3 (.in0(1'b1), .in1(Input[2]), .out(multiplexer_3_out), .sel(not_6_out));
  J_K_Flip_Flop j_k_ff_2 (
    .J(multiplexer_3_out), .clk(multiplexer_4_out), .K(multiplexer_2_out), .Q(out_4[2]));  // open: Qn, preset, en, reset
  Multiplexer #(.enable("false")) multiplexer_4 (
    .in0(j_k_ff_3_qn), .in1(Clock), .out(multiplexer_4_out), .sel(not_6_out));
  Multiplexer #(.enable("false")) multiplexer_5 (.in0(1'b1), .in1(not_4_out), .out(multiplexer_5_out), .sel(not_6_out));
  not not_4 (not_4_out, Input[1]);
  Multiplexer #(.enable("false")) multiplexer_6 (.in0(1'b1), .in1(Input[1]), .out(multiplexer_6_out), .sel(not_6_out));
  J_K_Flip_Flop j_k_ff_3 (
    .J(multiplexer_6_out), .clk(multiplexer_7_out), .K(multiplexer_5_out), .Q(out_4[1]), .Qn(j_k_ff_3_qn));  // open: preset, en, reset
  Multiplexer #(.enable("false")) multiplexer_7 (
    .in0(j_k_ff_4_qn), .in1(Clock), .out(multiplexer_7_out), .sel(not_6_out));
  not not_5 (not_5_out, Input[0]);
  Multiplexer #(.enable("false")) multiplexer_8 (.in0(1'b1), .in1(Input[0]), .out(multiplexer_8_out), .sel(not_6_out));
  Multiplexer #(.enable("false")) multiplexer_9 (.in0(1'b1), .in1(not_5_out), .out(multiplexer_9_out), .sel(not_6_out));
  J_K_Flip_Flop j_k_ff_4 (
    .J(multiplexer_8_out), .clk(multiplexer_10_out), .K(multiplexer_9_out), .Q(out_4[0]), .Qn(j_k_ff_4_qn));  // open: preset, en, reset
  not not_6 (not_6_out, Increment);
  Multiplexer #(.enable("false")) multiplexer_10 (
    .in0(Increment), .in1(Clock), .out(multiplexer_10_out), .sel(not_6_out));
endmodule
