// Logisim project Parts_CPU.circ as structural Verilog: 2 circuits, main circuit Register
module Register (
  input  Clock,
  input  R_0__W_1,
  input  [7:0] Input,
  output [7:0] Output
);

  wire and_1_out, and_2_out, and_3_out, and_4_out, and_5_out, and_6_out, and_7_out, and_8_out, and_9_out,
       and_10_out, and_11_out, and_12_out, and_13_out, and_14_out, and_15_out, and_16_out, j_k_ff_1_q,
       j_k_ff_2_q, j_k_ff_3_q, j_k_ff_4_q, j_k_ff_5_q, j_k_ff_6_q, j_k_ff_7_q, j_k_ff_8_q, not_1_out,
       not_2_out, not_3_out, not_4_out, not_5_out, not_6_out, not_7_out, not_8_out, not_9_out;

  not not_1 (not_1_out, R_0__W_1);
  not not_2 (not_2_out, Input[0]);
  not not_3 (not_3_out, Input[1]);
  not not_4 (not_4_out, Input[2]);
  not not_5 (not_5_out, Input[3]);
  not not_6 (not_6_out, Input[4]);
  not not_7 (not_7_out, Input[5]);
  not not_8 (not_8_out, Input[6]);
  not not_9 (not_9_out, Input[7]);
  and and_1 (and_1_out, R_0__W_1, Input[0]);
  and and_2 (and_2_out, R_0__W_1, not_2_out);
  and and_3 (and_3_out, R_0__W_1, Input[1]);
  and and_4 (and_4_out, R_0__W_1, not_3_out);
  and and_5 (and_5_out, R_0__W_1, Input[2]);
  and and_6 (and_6_out, R_0__W_1, not_4_out);
  and and_7 (and_7_out, R_0__W_1, Input[3]);
  and and_8 (and_8_out, R_0__W_1, not_5_out);
  and and_9 (and_9_out, R_0__W_1, Input[4]);
  and and_10 (and_10_out, R_0__W_1, not_6_out);
  and and_11 (and_11_out, R_0__W_1, Input[5]);
  and and_12 (and_12_out, R_0__W_1, not_7_out);
  and and_13 (and_13_out, R_0__W_1, Input[6]);
  and and_14 (and_14_out, R_0__W_1, not_8_out);
  and and_15 (and_15_out, R_0__W_1, Input[7]);
  and and_16 (and_16_out, R_0__W_1, not_9_out);
  J_K_Flip_Flop j_k_ff_1 (.J(and_1_out), .clk(Clock), .K(and_2_out), .Q(j_k_ff_1_q));  // open: Qn, preset, en, reset
  J_K_Flip_Flop j_k_ff_2 (.J(and_3_out), .clk(Clock), .K(and_4_out), .Q(j_k_ff_2_q));  // open: Qn, preset, en, reset
  J_K_Flip_Flop j_k_ff_3 (.J(and_5_out), .clk(Clock), .K(and_6_out), .Q(j_k_ff_3_q));  // open: Qn, preset, en, reset
  J_K_Flip_Flop j_k_ff_4 (.J(and_7_out), .clk(Clock), .K(and_8_out), .Q(j_k_ff_4_q));  // open: Qn, preset, en, reset
  J_K_Flip_Flop j_k_ff_5 (.J(and_9_out), .clk(Clock), .K(and_10_out), .Q(j_k_ff_5_q));  // open: Qn, preset, en, reset
  J_K_Flip_Flop j_k_ff_6 (.J(and_11_out), .clk(Clock), .K(and_12_out), .Q(j_k_ff_6_q));  // open: Qn, preset, en, reset
  J_K_Flip_Flop j_k_ff_7 (.J(and_13_out), .clk(Clock), .K(and_14_out), .Q(j_k_ff_7_q));  // open: Qn, preset, en, reset
  J_K_Flip_Flop j_k_ff_8 (.J(and_15_out), .clk(Clock), .K(and_16_out), .Q(j_k_ff_8_q));  // open: Qn, preset, en, reset
  and and_17 (Output[0], not_1_out, j_k_ff_1_q);
  and and_18 (Output[1], not_1_out, j_k_ff_2_q);
  and and_19 (Output[2], not_1_out, j_k_ff_3_q);
  and and_20 (Output[3], not_1_out, j_k_ff_4_q);
  and and_21 (Output[4], not_1_out, j_k_ff_5_q);
  and and_22 (Output[5], not_1_out, j_k_ff_6_q);
  and and_23 (Output[6], not_1_out, j_k_ff_7_q);
  and and_24 (Output[7], not_1_out, j_k_ff_8_q);
endmodule

module _4_bit_register__MAR (
  input  Clock,
  input  R_0__W_1,
  input  [3:0] Input,
  output [3:0] Output
);

  wire and_1_out, and_2_out, and_3_out, and_4_out, and_5_out, and_6_out, and_7_out, and_8_out, j_k_ff_1_q,
       j_k_ff_2_q, j_k_ff_3_q, j_k_ff_4_q, not_1_out, not_2_out, not_3_out, not_4_out, not_5_out;

  not not_1 (not_1_out, R_0__W_1);
  not not_2 (not_2_out, Input[0]);
  not not_3 (not_3_out, Input[1]);
  not not_4 (not_4_out, Input[2]);
  not not_5 (not_5_out, Input[3]);
  and and_1 (and_1_out, R_0__W_1, Input[0]);
  and and_2 (and_2_out, R_0__W_1, not_2_out);
  and and_3 (and_3_out, R_0__W_1, Input[1]);
  and and_4 (and_4_out, R_0__W_1, not_3_out);
  and and_5 (and_5_out, R_0__W_1, Input[2]);
  and and_6 (and_6_out, R_0__W_1, not_4_out);
  and and_7 (and_7_out, R_0__W_1, Input[3]);
  and and_8 (and_8_out, R_0__W_1, not_5_out);
  J_K_Flip_Flop j_k_ff_1 (.J(and_1_out), .clk(Clock), .K(and_2_out), .Q(j_k_ff_1_q));  // open: Qn, preset, en, reset
  J_K_Flip_Flop j_k_ff_2 (.J(and_3_out), .clk(Clock), .K(and_4_out), .Q(j_k_ff_2_q));  // open: Qn, preset, en, reset
  J_K_Flip_Flop j_k_ff_3 (.J(and_5_out), .clk(Clock), .K(and_6_out), .Q(j_k_ff_3_q));  // open: Qn, preset, en, reset
  J_K_Flip_Flop j_k_ff_4 (.J(and_7_out), .clk(Clock), .K(and_8_out), .Q(j_k_ff_4_q));  // open: Qn, preset, en, reset
  and and_9 (Output[0], not_1_out, j_k_ff_1_q);
  and and_10 (Output[1], not_1_out, j_k_ff_2_q);
  and and_11 (Output[2], not_1_out, j_k_ff_3_q);
  and and_12 (Output[3], not_1_out, j_k_ff_4_q);
endmodule
