// Logisim project Pete_RAM.circ as structural Verilog: 2 circuits, main circuit main
module main (
  input  Clock,
  input  Clear,
  input  R_W,
  input  [3:0] Address,
  input  [7:0] Data,
  output [7:0] Out
);

  wire demultiplexer_1_out0, demultiplexer_1_out1, demultiplexer_1_out2, demultiplexer_1_out3,
       demultiplexer_1_out4, demultiplexer_1_out5, demultiplexer_1_out6, demultiplexer_1_out7,
       demultiplexer_1_out8, demultiplexer_1_out9, demultiplexer_1_out10, demultiplexer_1_out11,
       demultiplexer_1_out12, demultiplexer_1_out13, demultiplexer_1_out14, demultiplexer_1_out15, or_1_out;
  wire [7:0] byte_1_output, byte_2_output, byte_3_output, byte_4_output, byte_5_output, byte_6_output,
       byte_7_output, byte_8_output, byte_9_output, byte_10_output, byte_11_output, byte_12_output,
       byte_13_output, byte_14_output, byte_15_output, byte_16_output, multiplexer_1_out;

  Multiplexer #(.width(8), .enable("false")) multiplexer_1 (
    .in0(Data), .in1({8{1'b0}}), .out(multiplexer_1_out), .sel(Clear));
  or or_1 (or_1_out, Clear, R_W);
  Demultiplexer #(.select(4), .enable("false")) demultiplexer_1 (
    .out0(demultiplexer_1_out0), .out1(demultiplexer_1_out1), .out2(demultiplexer_1_out2),
    .out3(demultiplexer_1_out3), .out4(demultiplexer_1_out4), .out5(demultiplexer_1_out5),
    .out6(demultiplexer_1_out6), .out7(demultiplexer_1_out7), .out8(demultiplexer_1_out8),
    .out9(demultiplexer_1_out9), .out10(demultiplexer_1_out10), .out11(demultiplexer_1_out11),
    .out12(demultiplexer_1_out12), .out13(demultiplexer_1_out13), .out14(demultiplexer_1_out14),
    .out15(demultiplexer_1_out15), .in(or_1_out), .sel(Address));
  \byte  byte_1 (
    .Clock(Clock), .R_0__W_1(demultiplexer_1_out0), .Clear(Clear), .Input(multiplexer_1_out),
    .Output(byte_1_output));
  \byte  byte_2 (
    .Clock(Clock), .R_0__W_1(demultiplexer_1_out1), .Clear(Clear), .Input(multiplexer_1_out),
    .Output(byte_2_output));
  \byte  byte_3 (
    .Clock(Clock), .R_0__W_1(demultiplexer_1_out2), .Clear(Clear), .Input(multiplexer_1_out),
    .Output(byte_3_output));
  \byte  byte_4 (
    .Clock(Clock), .R_0__W_1(demultiplexer_1_out3), .Clear(Clear), .Input(multiplexer_1_out),
    .Output(byte_4_output));
  \byte  byte_5 (
    .Clock(Clock), .R_0__W_1(demultiplexer_1_out4), .Clear(Clear), .Input(multiplexer_1_out),
    .Output(byte_5_output));
  \byte  byte_6 (
    .Clock(Clock), .R_0__W_1(demultiplexer_1_out5), .Clear(Clear), .Input(multiplexer_1_out),
    .Output(byte_6_output));
  \byte  byte_7 (
    .Clock(Clock), .R_0__W_1(demultiplexer_1_out6), .Clear(Clear), .Input(multiplexer_1_out),
    .Output(byte_7_output));
  \byte  byte_8 (
    .Clock(Clock), .R_0__W_1(demultiplexer_1_out7), .Clear(Clear), .Input(multiplexer_1_out),
    .Output(byte_8_output));
  \byte  byte_9 (
    .Clock(Clock), .R_0__W_1(demultiplexer_1_out8), .Clear(Clear), .Input(multiplexer_1_out),
    .Output(byte_9_output));
  \byte  byte_10 (
    .Clock(Clock), .R_0__W_1(demultiplexer_1_out9), .Clear(Clear), .Input(multiplexer_1_out),
    .Output(byte_10_output));
  \byte  byte_11 (
    .Clock(Clock), .R_0__W_1(demultiplexer_1_out10), .Clear(Clear), .Input(multiplexer_1_out),
    .Output(byte_11_output));
  \byte  byte_12 (
    .Clock(Clock), .R_0__W_1(demultiplexer_1_out11), .Clear(Clear), .Input(multiplexer_1_out),
    .Output(byte_12_output));
  \byte  byte_13 (
    .Clock(Clock), .R_0__W_1(demultiplexer_1_out12), .Clear(Clear), .Input(multiplexer_1_out),
    .Output(byte_13_output));
  \byte  byte_14 (
    .Clock(Clock), .R_0__W_1(demultiplexer_1_out13), .Clear(Clear), .Input(multiplexer_1_out),
    .Output(byte_14_output));
  \byte  byte_15 (
    .Clock(Clock), .R_0__W_1(demultiplexer_1_out14), .Clear(Clear), .Input(multiplexer_1_out),
    .Output(byte_15_output));
  \byte  byte_16 (
    .Clock(Clock), .R_0__W_1(demultiplexer_1_out15), .Clear(Clear), .Input(multiplexer_1_out),
    .Output(byte_16_output));
  Multiplexer #(.select(4), .width(8), .enable("false")) multiplexer_2 (
    .in0(byte_1_output), .in1(byte_2_output), .in2(byte_3_output), .in3(byte_4_output), .in4(byte_5_output),
    .in5(byte_6_output), .in6(byte_7_output), .in7(byte_8_output), .in8(byte_9_output), .in9(byte_10_output),
    .in10(byte_11_output), .in11(byte_12_output), .in12(byte_13_output), .in13(byte_14_output),
    .in14(byte_15_output), .in15(byte_16_output), .out(Out), .sel(Address));
endmodule

module \byte  (
  input  Clock,
  input  R_0__W_1,
  input  Clear,
  input  [7:0] Input,
  output [7:0] Output
);

  wire and_1_out, and_2_out, and_3_out, and_4_out, and_5_out, and_6_out, and_7_out, and_8_out, and_9_out,
       and_10_out, and_11_out, and_12_out, and_13_out, and_14_out, and_15_out, and_16_out, j_k_ff_1_q,
       j_k_ff_2_q, j_k_ff_3_q, j_k_ff_4_q, j_k_ff_5_q, j_k_ff_6_q, j_k_ff_7_q, j_k_ff_8_q, not_1_out,
       not_2_out, not_3_out, not_4_out, not_5_out, not_6_out, not_7_out, not_8_out, not_9_out, or_1_out;

  or or_1 (or_1_out, R_0__W_1, Clear);
  not not_1 (not_1_out, or_1_out);
  not not_2 (not_2_out, Input[7]);
  not not_3 (not_3_out, Input[6]);
  not not_4 (not_4_out, Input[5]);
  not not_5 (not_5_out, Input[4]);
  not not_6 (not_6_out, Input[3]);
  not not_7 (not_7_out, Input[2]);
  not not_8 (not_8_out, Input[1]);
  not not_9 (not_9_out, Input[0]);
  and and_1 (and_1_out, or_1_out, Input[7]);
  and and_2 (and_2_out, or_1_out, not_2_out);
  and and_3 (and_3_out, or_1_out, Input[6]);
  and and_4 (and_4_out, or_1_out, not_3_out);
  and and_5 (and_5_out, or_1_out, Input[5]);
  and and_6 (and_6_out, or_1_out, not_4_out);
  and and_7 (and_7_out, or_1_out, Input[4]);
  and and_8 (and_8_out, or_1_out, not_5_out);
  and and_9 (and_9_out, or_1_out, Input[3]);
  and and_10 (and_10_out, or_1_out, not_6_out);
  and and_11 (and_11_out, or_1_out, Input[2]);
  and and_12 (and_12_out, or_1_out, not_7_out);
  and and_13 (and_13_out, or_1_out, Input[1]);
  and and_14 (and_14_out, or_1_out, not_8_out);
  and and_15 (and_15_out, or_1_out, Input[0]);
  and and_16 (and_16_out, or_1_out, not_9_out);
  J_K_Flip_Flop j_k_ff_1 (.J(and_1_out), .clk(Clock), .K(and_2_out), .Q(j_k_ff_1_q));  // open: Qn, preset, en, reset
  J_K_Flip_Flop j_k_ff_2 (.J(and_3_out), .clk(Clock), .K(and_4_out), .Q(j_k_ff_2_q));  // open: Qn, preset, en, reset
  J_K_Flip_Flop j_k_ff_3 (.J(and_5_out), .clk(Clock), .K(and_6_out), .Q(j_k_ff_3_q));  // open: Qn, preset, en, reset
  J_K_Flip_Flop j_k_ff_4 (.J(and_7_out), .clk(Clock), .K(and_8_out), .Q(j_k_ff_4_q));  // open: Qn, preset, en, reset
  J_K_Flip_Flop j_k_ff_5 (.J(and_9_out), .clk(Clock), .K(and_10_out), .Q(j_k_ff_5_q));  // open: Qn, preset, en, reset
  J_K_Flip_Flop j_k_ff_6 (.J(and_11_out), .clk(Clock), .K(and_12_out), .Q(j_k_ff_6_q));  // open: Qn, preset, en, reset
  J_K_Flip_Flop j_k_ff_7 (.J(and_13_out), .clk(Clock), .K(and_14_out), .Q(j_k_ff_7_q));  // open: Qn, preset, en, reset
  J_K_Flip_Flop j_k_ff_8 (.J(and_15_out), .clk(Clock), .K(and_16_out), .Q(j_k_ff_8_q));  // open: Qn, preset, en, reset
  and and_17 (Output[7], not_1_out, j_k_ff_1_q);
  and and_18 (Output[6], not_1_out, j_k_ff_2_q);
  and and_19 (Output[5], not_1_out, j_k_ff_3_q);
  and and_20 (Output[4], not_1_out, j_k_ff_4_q);
  and and_21 (Output[3], not_1_out, j_k_ff_5_q);
  and and_22 (Output[2], not_1_out, j_k_ff_6_q);
  and and_23 (Output[1], not_1_out, j_k_ff_7_q);
  and and_24 (Output[0], not_1_out, j_k_ff_8_q);
endmodule
