// Logisim project alu.circ as structural Verilog: 5 circuits, main circuit main
module main (
  input  [7:0] A,
  input  in_2,
  input  R_W,
  input  [7:0] B,
  input  Add_0_Sub_1,
  output are_equal,
  output Zero,
  output Negative,
  output [7:0] Result,
  output Carry,
  output Overflow
);

  wire or_1_out;
  wire [6:0] multiplexer_2_out;
  wire [7:0] multiplexer_1_out, n4_bit_adder_subtracter_1_result, n4_bit_and_1_out_3, n4_bit_or_1_out_3;

  _4_bit_AND u_4_bit_and_1 (.in_1(A), .out_3(n4_bit_and_1_out_3), .in_2(B));
  _4_bit_OR u_4_bit_or_1 (.in_1(A), .out_3(n4_bit_or_1_out_3), .in_2(B));
  _4_bit_Adder_Subtracter u_4_bit_adder_subtracter_1 (
    .Add_Sub_Control(Add_0_Sub_1), .Result(n4_bit_adder_subtracter_1_result), .A(A), .B(B),
    .Carry_out(Carry), .Overflow(Overflow));
  Multiplexer #(.width(8), .enable("false")) multiplexer_1 (
    .in0(n4_bit_and_1_out_3), .in1(n4_bit_or_1_out_3), .out(multiplexer_1_out), .sel(Add_0_Sub_1));
  Multiplexer #(.width(8), .enable("false")) multiplexer_2 (
    .in0(multiplexer_1_out), .in1(n4_bit_adder_subtracter_1_result), .out({Negative, multiplexer_2_out}),
    .sel(1'b1));
  and and_1 (are_equal, n4_bit_and_1_out_3[0], n4_bit_and_1_out_3[1], n4_bit_and_1_out_3[2], n4_bit_and_1_out_3[3], n4_bit_and_1_out_3[4], n4_bit_and_1_out_3[5], n4_bit_and_1_out_3[6], n4_bit_and_1_out_3[7]);
  // Probe on {Negative, multiplexer_2_out}
  or or_1 (or_1_out, multiplexer_2_out[0], multiplexer_2_out[1], multiplexer_2_out[2], multiplexer_2_out[3], multiplexer_2_out[4], multiplexer_2_out[5], multiplexer_2_out[6], Negative);
  not not_1 (Zero, or_1_out);
  Register register_1 (.Clock(in_2), .R_0__W_1(R_W), .Input({Negative, multiplexer_2_out}), .Output(Result));

  // Notes on the sheet:
  //   AND
  //   OR
  //   +/-
  //   Select AND (0) or OR (1)
  //   Select ADD (0) or SUB (1)
  //   Select Logic (0) or Math (1)
endmodule

// +
module _1_bit_Adder (
  input  Carry_In,
  input  A,
  input  B,
  output Result,
  output Carry_Out
);

  wire and_1_out, and_2_out, xor_1_out;

  and and_1 (and_1_out, A, B);
  xor xor_1 (xor_1_out, A, B);
  or or_1 (Carry_Out, and_1_out, and_2_out);
  and and_2 (and_2_out, Carry_In, xor_1_out);
  xor xor_2 (Result, Carry_In, xor_1_out);

  // Notes on the sheet:
  //   Full Adder
endmodule

module _4_bit_Adder_Subtracter (
  input  Add_Sub_Control,
  input  [7:0] A,
  input  [7:0] B,
  output [7:0] Result,
  output Carry_out,
  output Overflow
);

  wire adder_1_cout, adder_2_cout, adder_3_cout, adder_4_cout, adder_5_cout, adder_6_cout, adder_7_cout,
       and_1_out, and_2_out, not_1_out, not_2_out, not_3_out, xor_1_out, xor_2_out, xor_3_out, xor_4_out,
       xor_5_out, xor_6_out, xor_7_out, xor_8_out;

  // Probe on A
  // Probe on B
  xor xor_1 (xor_1_out, Add_Sub_Control, B[0]);
  xor xor_2 (xor_2_out, Add_Sub_Control, B[1]);
  xor xor_3 (xor_3_out, Add_Sub_Control, B[2]);
  xor xor_4 (xor_4_out, Add_Sub_Control, B[3]);
  xor xor_5 (xor_5_out, Add_Sub_Control, B[4]);
  xor xor_6 (xor_6_out, Add_Sub_Control, B[5]);
  xor xor_7 (xor_7_out, Add_Sub_Control, B[6]);
  xor xor_8 (xor_8_out, Add_Sub_Control, B[7]);
  not not_1 (not_1_out, xor_8_out);
  not not_2 (not_2_out, A[7]);
  Adder #(.width(1)) adder_1 (.a(A[0]), .b(xor_1_out), .out(Result[0]), .cin(Add_Sub_Control), .cout(adder_1_cout));
  Adder #(.width(1)) adder_2 (.a(A[1]), .b(xor_2_out), .out(Result[1]), .cin(adder_1_cout), .cout(adder_2_cout));
  Adder #(.width(1)) adder_3 (.a(A[2]), .b(xor_3_out), .out(Result[2]), .cin(adder_2_cout), .cout(adder_3_cout));
  Adder #(.width(1)) adder_4 (.a(A[3]), .b(xor_4_out), .out(Result[3]), .cin(adder_3_cout), .cout(adder_4_cout));
  Adder #(.width(1)) adder_5 (.a(A[4]), .b(xor_5_out), .out(Result[4]), .cin(adder_4_cout), .cout(adder_5_cout));
  Adder #(.width(1)) adder_6 (.a(A[5]), .b(xor_6_out), .out(Result[5]), .cin(adder_5_cout), .cout(adder_6_cout));
  Adder #(.width(1)) adder_7 (.a(A[6]), .b(xor_7_out), .out(Result[6]), .cin(adder_6_cout), .cout(adder_7_cout));
  Adder #(.width(1)) adder_8 (.a(A[7]), .b(xor_8_out), .out(Result[7]), .cin(adder_7_cout), .cout(Carry_out));
  not not_3 (not_3_out, Result[7]);
  // Probe on Result
  and and_1 (and_1_out, Result[7], not_2_out, not_1_out);
  and and_2 (and_2_out, not_3_out, A[7], xor_8_out);
  or or_1 (Overflow, and_1_out, and_2_out);
endmodule

module _4_bit_AND (
  input  [7:0] in_1,
  input  [7:0] in_2,
  output [7:0] out_3
);

  xnor xnor_1 (out_3[0], in_1[0], in_2[0]);
  xnor xnor_2 (out_3[1], in_1[1], in_2[1]);
  xnor xnor_3 (out_3[2], in_1[2], in_2[2]);
  xnor xnor_4 (out_3[3], in_1[3], in_2[3]);
  xnor xnor_5 (out_3[4], in_1[4], in_2[4]);
  xnor xnor_6 (out_3[5], in_1[5], in_2[5]);
  xnor xnor_7 (out_3[6], in_1[6], in_2[6]);
  xnor xnor_8 (out_3[7], in_1[7], in_2[7]);
endmodule

module _4_bit_OR (
  input  [7:0] in_1,
  input  [7:0] in_2,
  output [7:0] out_3
);

  or or_1 (out_3[0], in_1[0], in_2[0]);
  or or_2 (out_3[1], in_1[1], in_2[1]);
  or or_3 (out_3[2], in_1[2], in_2[2]);
  or or_4 (out_3[3], in_1[3], in_2[3]);
  or or_5 (out_3[4], in_1[4], in_2[4]);
  or or_6 (out_3[5], in_1[5], in_2[5]);
  or or_7 (out_3[6], in_1[6], in_2[6]);
  or or_8 (out_3[7], in_1[7], in_2[7]);
endmodule
