// Logisim project keypad black box.circ as structural Verilog: 1 circuit, main circuit keypadblackbox
module keypadblackbox (
  input  in_1,
  input  in_2,
  input  in_3,
  input  in_4,
  input  in_5,
  input  in_6,
  input  in_7,
  input  in_8,
  input  in_9,
  input  in_10,
  output [7:0] out_11
);

  wire and_1_out, and_2_out, and_3_out, and_4_out, and_5_out, and_6_out, and_7_out, and_8_out, clk,
       nor_2_out, nor_4_out, nor_6_out, nor_8_out, not_12_out, not_13_out, not_14_out, not_15_out;
  wire [2:1] not_10_out;
  wire [2:2] not_9_out;
  wire [3:0] demultiplexer_1_out1, demultiplexer_2_out1, demultiplexer_3_out1, demultiplexer_4_out1,
       demultiplexer_5_out1, demultiplexer_6_out1, demultiplexer_7_out1, demultiplexer_8_out1,
       demultiplexer_9_out0, demultiplexer_9_out1, demultiplexer_10_out1, multiplexer_1_out, selector;
  wire [3:3] not_1_out, not_2_out, not_3_out, not_4_out, not_5_out, not_6_out, not_7_out, not_8_out;

  not not_1 (not_1_out[3], 1'b1);
  not not_2 (not_2_out[3], 1'b1);
  not not_3 (not_3_out[3], 1'b1);
  not not_4 (not_4_out[3], 1'b1);
  not not_5 (not_5_out[3], 1'b1);
  not not_6 (not_6_out[3], 1'b1);
  not not_7 (not_7_out[3], 1'b1);
  not not_8 (not_8_out[3], 1'b1);
  not not_9 (not_9_out[2], 1'b1);
  not not_10 (not_10_out[1], 1'b1);
  not not_11 (not_10_out[2], 1'b1);
  Demultiplexer #(.width(4), .enable("false")) demultiplexer_1 (
    .out1(demultiplexer_1_out1), .in({4{not_1_out[3]}}), .sel(in_1));  // open: out0
  Demultiplexer #(.width(4), .enable("false")) demultiplexer_2 (
    .out1(demultiplexer_2_out1), .in({{2{not_4_out[3]}}, 2'b11}), .sel(in_4));  // open: out0
  Demultiplexer #(.width(4), .enable("false")) demultiplexer_3 (
    .out1(demultiplexer_3_out1), .in({not_7_out[3], 2'b11, not_7_out[3]}), .sel(in_7));  // open: out0
  Demultiplexer #(.width(4), .enable("false")) demultiplexer_4 (
    .out1(demultiplexer_4_out1), .in({{3{not_2_out[3]}}, 1'b1}), .sel(in_2));  // open: out0
  Demultiplexer #(.width(4), .enable("false")) demultiplexer_5 (
    .out1(demultiplexer_5_out1), .in({not_5_out[3], 1'b1, {2{not_5_out[3]}}}), .sel(in_5));  // open: out0
  Demultiplexer #(.width(4), .enable("false")) demultiplexer_6 (
    .out1(demultiplexer_6_out1), .in({not_8_out[3], 3'b111}), .sel(in_8));  // open: out0
  Multiplexer #(.select(4), .width(4), .enable("false")) multiplexer_1 (
    .in0({4{not_1_out[3]}}), .in1({{3{not_2_out[3]}}, 1'b1}), .in2({{2{not_3_out[3]}}, 1'b1, not_3_out[3]}),
    .in3({{2{not_4_out[3]}}, 2'b11}), .in4({not_5_out[3], 1'b1, {2{not_5_out[3]}}}),
    .in5({not_6_out[3], 1'b1, not_6_out[3], 1'b1}), .in6({not_7_out[3], 2'b11, not_7_out[3]}),
    .in7({not_8_out[3], 3'b111}), .in8({1'b1, {3{not_9_out[2]}}}), .in9({1'b1, not_10_out, 1'b1}),
    .out(multiplexer_1_out), .sel(selector));  // open: in10, in11, in12, in13, in14, in15
  Demultiplexer #(.width(4), .enable("false")) demultiplexer_7 (
    .out1(demultiplexer_7_out1), .in({1'b1, {3{not_9_out[2]}}}), .sel(in_9));  // open: out0
  Demultiplexer #(.width(4), .enable("false")) demultiplexer_8 (
    .out1(demultiplexer_8_out1), .in({1'b1, not_10_out, 1'b1}), .sel(in_10));  // open: out0
  Demultiplexer #(.width(4), .enable("false")) demultiplexer_9 (
    .out0(demultiplexer_9_out0), .out1(demultiplexer_9_out1), .in({{2{not_3_out[3]}}, 1'b1, not_3_out[3]}),
    .sel(in_3));
  Demultiplexer #(.width(4), .enable("false")) demultiplexer_10 (
    .out1(demultiplexer_10_out1), .in({not_6_out[3], 1'b1, not_6_out[3], 1'b1}), .sel(in_6));  // open: out0
  assign selector = demultiplexer_1_out1 | demultiplexer_4_out1 | demultiplexer_9_out1 | demultiplexer_2_out1 | demultiplexer_10_out1 | demultiplexer_5_out1 | demultiplexer_3_out1 | demultiplexer_6_out1 | demultiplexer_7_out1 | demultiplexer_8_out1;  // OR_Gate or_1, 4 bits wide
  or u_clk (clk, in_1, in_2, in_3, in_4, in_5, in_6, in_7, in_8, in_9, in_10);
  // Probe on selector
  and and_1 (and_1_out, clk, not_12_out);
  not not_12 (not_12_out, multiplexer_1_out[0]);
  and and_2 (and_2_out, clk, multiplexer_1_out[0]);
  not not_13 (not_13_out, multiplexer_1_out[1]);
  and and_3 (and_3_out, clk, not_14_out);
  not not_14 (not_14_out, multiplexer_1_out[2]);
  and and_4 (and_4_out, clk, multiplexer_1_out[2]);
  not not_15 (not_15_out, multiplexer_1_out[3]);
  and and_5 (and_5_out, clk, not_13_out);
  and and_6 (and_6_out, clk, multiplexer_1_out[1]);
  and and_7 (and_7_out, clk, not_15_out);
  and and_8 (and_8_out, clk, multiplexer_1_out[3]);
  nor nor_1 (out_11[0], and_1_out, nor_2_out);
  nor nor_2 (nor_2_out, out_11[0], and_2_out);
  nor nor_3 (out_11[1], and_5_out, nor_4_out);
  nor nor_4 (nor_4_out, out_11[1], and_6_out);
  nor nor_5 (out_11[2], and_3_out, nor_6_out);
  nor nor_6 (nor_6_out, out_11[2], and_4_out);
  nor nor_7 (out_11[3], and_7_out, nor_8_out);
  nor nor_8 (nor_8_out, out_11[3], and_8_out);

  assign out_11[7:4] = 4'b0000;
endmodule
