// Logisim project keypad.circ as structural Verilog: 1 circuit, main circuit main
module main (
);

  wire _0_out, _1_out, _2_out, _3_out, _4_out, _5_out, _6_out, _7_out, _8_out, _9_out;
  wire [7:0] main_1_out_12;

  Button _1 (.out(_1_out));
  Button _2 (.out(_2_out));
  Button _5 (.out(_5_out));
  Button _4 (.out(_4_out));
  Button _8 (.out(_8_out));
  Button _7 (.out(_7_out));
  Button _0 (.out(_0_out));
  Button _3 (.out(_3_out));
  Button _6 (.out(_6_out));
  Button _9 (.out(_9_out));
  keypad_black_box_main main_1 (
    .in_1(_0_out), .in_2(_1_out), .in_3(_2_out), .in_4(_3_out), .in_5(_4_out), .in_6(_5_out), .in_7(_6_out),
    .in_8(_7_out), .in_9(_8_out), .in_10(_9_out), .out_12(main_1_out_12));  // open: out_11
  // Probe on main_1_out_12
endmodule
