// Logisim project multiplier.circ as structural Verilog: 1 circuit, main circuit main
module main (
  input  [7:0] in_1,
  input  [7:0] in_2,
  output [7:0] out_3,
  output out_4
);

  wire [7:0] adder_7_out;
  wire [15:0] adder_1_out, adder_2_out, adder_3_out, adder_4_out, adder_5_out, adder_6_out,
       multiplexer_1_out, multiplexer_2_out, multiplexer_3_out, multiplexer_4_out, multiplexer_5_out,
       multiplexer_6_out, multiplexer_7_out, multiplexer_8_out;

  Multiplexer #(.width(16), .enable("false")) multiplexer_1 (
    .in0({16{1'b0}}), .in1({{8{1'b0}}, in_1}), .out(multiplexer_1_out), .sel(in_2[0]));
  Multiplexer #(.width(16), .enable("false")) multiplexer_2 (
    .in0({16{1'b0}}), .in1({{7{1'b0}}, in_1, 1'b0}), .out(multiplexer_2_out), .sel(in_2[1]));
  Multiplexer #(.width(16), .enable("false")) multiplexer_3 (
    .in0({16{1'b0}}), .in1({{6{1'b0}}, in_1, 2'b00}), .out(multiplexer_3_out), .sel(in_2[2]));
  Multiplexer #(.width(16), .enable("false")) multiplexer_4 (
    .in0({16{1'b0}}), .in1({{5{1'b0}}, in_1, 3'b000}), .out(multiplexer_4_out), .sel(in_2[3]));
  Multiplexer #(.width(16), .enable("false")) multiplexer_5 (
    .in0({16{1'b0}}), .in1({4'b0000, in_1, 4'b0000}), .out(multiplexer_5_out), .sel(in_2[4]));
  Multiplexer #(.width(16), .enable("false")) multiplexer_6 (
    .in0({16{1'b0}}), .in1({3'b000, in_1, {5{1'b0}}}), .out(multiplexer_6_out), .sel(in_2[5]));
  Multiplexer #(.width(16), .enable("false")) multiplexer_7 (
    .in0({16{1'b0}}), .in1({2'b00, in_1, {6{1'b0}}}), .out(multiplexer_7_out), .sel(in_2[6]));
  Multiplexer #(.width(16), .enable("false")) multiplexer_8 (
    .in0({16{1'b0}}), .in1({1'b0, in_1, {7{1'b0}}}), .out(multiplexer_8_out), .sel(in_2[7]));
  // Probe on multiplexer_1_out
  // Probe on multiplexer_2_out
  // Probe on multiplexer_3_out
  // Probe on multiplexer_4_out
  // Probe on multiplexer_5_out
  // Probe on multiplexer_6_out
  // Probe on multiplexer_7_out
  // Probe on multiplexer_8_out
  or or_1 (out_4, adder_7_out[0], adder_7_out[1], adder_7_out[2], adder_7_out[3], adder_7_out[4], adder_7_out[5], adder_7_out[6], adder_7_out[7]);
  Adder #(.width(16)) adder_1 (.a(multiplexer_1_out), .b(multiplexer_2_out), .out(adder_1_out));  // open: cin, cout
  Adder #(.width(16)) adder_2 (.a(adder_1_out), .b(multiplexer_3_out), .out(adder_2_out));  // open: cin, cout
  Adder #(.width(16)) adder_3 (.a(adder_2_out), .b(multiplexer_4_out), .out(adder_3_out));  // open: cin, cout
  Adder #(.width(16)) adder_4 (.a(adder_3_out), .b(multiplexer_5_out), .out(adder_4_out));  // open: cin, cout
  Adder #(.width(16)) adder_5 (.a(adder_4_out), .b(multiplexer_6_out), .out(adder_5_out));  // open: cin, cout
  Adder #(.width(16)) adder_6 (.a(adder_5_out), .b(multiplexer_7_out), .out(adder_6_out));  // open: cin, cout
  Adder #(.width(16)) adder_7 (.a(adder_6_out), .b(multiplexer_8_out), .out({adder_7_out, out_3}));  // open: cin, cout
  // Probe on adder_1_out
  // Probe on adder_2_out
  // Probe on adder_3_out
  // Probe on adder_4_out
  // Probe on adder_5_out
  // Probe on adder_6_out
  // Probe on {adder_7_out, out_3}
endmodule
