// Logisim project shift3_display.circ as structural Verilog: 1 circuit, main circuit main
module main (
  input  in_1,
  input  in_2,
  input  in_3,
  input  in_4,
  output out_5,
  output out_6,
  output out_7,
  output out_8
);

  wire or_7_out;
  wire [1:0] not_1_out;
  wire [3:0] adder_1_out, demultiplexer_1_out0, demultiplexer_1_out1, demultiplexer_1_out2,
       demultiplexer_1_out3, demultiplexer_1_out4, demultiplexer_1_out5, demultiplexer_1_out6,
       demultiplexer_1_out7, demultiplexer_1_out8, demultiplexer_1_out9, demultiplexer_1_out10,
       demultiplexer_2_out1, or_4_out, or_5_out;

  or or_1 (out_5, or_4_out[3], demultiplexer_2_out1[3]);
  Demultiplexer #(.select(4), .width(4), .disabled(0), .enable("false")) demultiplexer_1 (
    .out0(demultiplexer_1_out0), .out1(demultiplexer_1_out1), .out2(demultiplexer_1_out2),
    .out3(demultiplexer_1_out3), .out4(demultiplexer_1_out4), .out5(demultiplexer_1_out5),
    .out6(demultiplexer_1_out6), .out7(demultiplexer_1_out7), .out8(demultiplexer_1_out8),
    .out9(demultiplexer_1_out9), .out10(demultiplexer_1_out10), .in({in_1, in_2, in_3, in_4}),
    .sel({in_1, in_2, in_3, in_4}));  // open: out11, out12, out13, out14, out15
  or or_2 (out_6, or_4_out[2], demultiplexer_2_out1[2]);
  // Probe on demultiplexer_1_out9
  not not_1 (not_1_out[0], 1'b0);
  not not_2 (not_1_out[1], 1'b0);
  or or_3 (out_7, or_4_out[1], demultiplexer_2_out1[1]);
  assign or_4_out = demultiplexer_1_out0 | demultiplexer_1_out1 | demultiplexer_1_out2 | demultiplexer_1_out3 | demultiplexer_1_out4;  // OR_Gate or_4, 4 bits wide
  assign or_5_out = demultiplexer_1_out5 | demultiplexer_1_out6 | demultiplexer_1_out7 | demultiplexer_1_out8 | demultiplexer_1_out9;  // OR_Gate or_5, 4 bits wide
  Adder #(.width(4)) adder_1 (.a(or_5_out), .b({2'b00, not_1_out}), .out(adder_1_out));  // open: cin, cout
  or or_6 (out_8, or_4_out[0], demultiplexer_2_out1[0]);
  or or_7 (or_7_out, or_5_out[3], or_5_out[2], or_5_out[1], or_5_out[0]);
  Demultiplexer #(.width(4), .enable("false")) demultiplexer_2 (
    .out1(demultiplexer_2_out1), .in(adder_1_out), .sel(or_7_out));  // open: out0

  // Notes on the sheet:
  //   input for add 3 if greater than 5
endmodule
